// Digital circuit ALU.dig as structural Verilog
module ALU (
  input  nCin,
  input  C_sel,
  input  C_val,
  input  [15:0] A,
  input  [15:0] B,
  input  M,
  input  [3:0] Sel,
  output Z_f,
  output [15:0] Sum,
  output N_f,
  output V_f,
  output C_f
);

  wire _7408_1_p1, _7408_1_p2, _7408_1_p3, _7408_1_p4, _7408_1_p6, _7408_1_p7, _7408_2_p2, _7408_2_p4,
       _7408_2_p6, _7408_2_p8, _7408_2_p9, _7408_2_p10, _7408_2_p11, _7408_2_p12, _74181_1_p6, _74181_1_p8,
       _74181_2_p7, _74181_2_p9, _74181_3_p7, _74181_3_p9, _74182_1_p2, _74182_1_p4, C_n, C_n_plus_x,
       C_n_plus_y, C_n_plus_z;

  // _74151 _74151_1: pin names not known; wires that end beside it: C_n, C_sel, 1'b0, 1'b0, 1'b0, C_val, nCin, 1'b0, 1'b0, 1'b0
  // _74181 _74181_1: pin names not known; wires that end beside it: 1'b0, 1'b0, 1'b0, 1'b1, 1'b0, _74181_1_p6, C_n_plus_z, _74181_1_p8, A[12], Sum[12], A[13], Sum[13], A[14], Sum[14], A[15], N_f, B[12], B[13], C_f, B[14], B[15], Sel[0]
  // _74181 _74181_2: pin names not known; wires that end beside it: Sel[1], Sel[2], Sel[3], M, 1'b1, 1'b0, _74181_2_p7, C_n_plus_y, _74181_2_p9, A[8], Sum[8], A[9], Sum[9], A[10], Sum[10], A[11], Sum[11], B[8], B[9], B[10], B[11], Sel[0]
  // _74181 _74181_3: pin names not known; wires that end beside it: Sel[1], Sel[2], Sel[3], M, 1'b1, 1'b0, _74181_3_p7, C_n_plus_x, _74181_3_p9, A[4], Sum[4], A[5], Sum[5], A[6], Sum[6], A[7], Sum[7], B[4], B[5], B[6], B[7], Sel[0]
  // _74182 _74182_1: pin names not known; wires that end beside it: C_n, _74182_1_p2, C_n_plus_z, _74182_1_p4, C_n_plus_y, _74181_3_p7, C_n_plus_x, _74181_3_p9, _74181_2_p7, _74181_2_p9, _74181_1_p6, _74181_1_p8, 1'b1, 1'b0
  // _74181 _74181_4: pin names not known; wires that end beside it: Sel[1], Sel[2], Sel[3], M, 1'b1, 1'b0, _74182_1_p2, C_n, _74182_1_p4, A[0], Sum[0], A[1], Sum[1], A[2], Sum[2], A[3], Sum[3], B[0], B[1], B[2], B[3], Sel[0], Sel[1]
  // _7408 _7408_1: pin names not known; wires that end beside it: _7408_1_p1, _7408_1_p2, _7408_1_p3, _7408_1_p4, Z_f, _7408_1_p6, _7408_1_p7, _7408_1_p1, _7408_1_p3, 1'b0, 1'b0, 1'b1, 1'b0
  // _7408 _7408_2: pin names not known; wires that end beside it: _7408_1_p2, _7408_2_p2, _7408_1_p4, _7408_2_p4, _7408_1_p6, _7408_2_p6, _7408_1_p7, _7408_2_p8, _7408_2_p9, _7408_2_p10, _7408_2_p11, _7408_2_p12, 1'b1, 1'b0
  // _7402 NOR: pin names not known; wires that end beside it: Sel[2], Sel[3], M, 1'b1, 1'b0, _7408_2_p2, Sum[12], _7408_2_p4, Sum[13], _7408_2_p6, Sum[14], _7408_2_p8, N_f, Sum[8], Sum[9], Sum[10], Sum[11]
  // _7402 NOR_2: pin names not known; wires that end beside it: 1'b1, 1'b0, _7408_2_p9, Sum[4], _7408_2_p10, Sum[5], _7408_2_p11, Sum[6], _7408_2_p12, Sum[7], Sum[0], Sum[1], Sum[2], Sum[3]
  // _74151 OVF: pin names not known; wires that end beside it: 1'b1, 1'b0, V_f, A[15], N_f, B[15], 1'b0, 1'b0, Sel[1], 1'b0, Sel[0], Sel[0], 1'b0, Sel[1], 1'b0, 1'b1, 1'b0

  assign Sum[15] = N_f;

  // Other names for the same wires on the sheet: F_1[3:0] = Sum[7:4]; F_0[3:0] = Sum[3:0]; F_2[3:0] = Sum[11:8];
  //   F_3[3:0] = {N_f, Sum[14:12]}; F15 = N_f; S[3:0] = Sel
endmodule
