// Digital circuit ALU4.dig as structural Verilog
module ALU4 (
  input  [7:0] A,
  input  [7:0] B,
  input  [4:0] Sel,
  input  Ci,
  output [7:0] F,
  output A_eq_B,
  output C
);

  wire _74181_1_p21, _74181_1_p22, _74181_2_p21;

  // _74181 _74181_1: pin names not known; wires that end beside it: Ci, A[0], A[1], A[2], A[3], B[0], B[1], B[2], B[3], Sel[0], Sel[1], Sel[2], Sel[3], Sel[4], 1'b1, 1'b0, F[0], F[1], F[2], F[3], _74181_1_p21, _74181_1_p22
  // _74181 _74181_2: pin names not known; wires that end beside it: _74181_1_p22, A[4], A[5], A[6], A[7], B[4], B[5], B[6], B[7], Sel[0], Sel[1], Sel[2], Sel[3], Sel[4], 1'b1, 1'b0, F[4], F[5], F[6], F[7], _74181_2_p21, C
  and and_1 (A_eq_B, _74181_1_p21, _74181_2_p21);
endmodule
