// Digital circuit ALU_old.dig as structural Verilog
module ALU_old (
  input  [7:0] B,
  input  [3:0] SEL,
  input  M,
  input  [7:0] A,
  input  nCin,
  input  C_sel,
  input  C_val,
  input  nALU_Fout,
  input  rot,
  output V_f,
  output Z_f,
  output N_f,
  output C_f,
  output [7:0] Sum
);

  wire _74151_1_p1, _74181_1_p3, _74181_2_p19, AND_p2, AND_p4, AND_p6, C, OVF_p3, pulldown_1_out;
  wire [3:0] NOR_p7;

  // _74151 _74151_1: pin names not known; wires that end beside it: _74151_1_p1, C_sel, 1'b0, 1'b0, 1'b0, C_val, nCin, 1'b0, 1'b0, 1'b0, 1'b0, 1'b0, 1'b0, 1'b1, 1'b0
  PullDown pulldown_1 (.out(pulldown_1_out));
  // _7402 NOR: pin names not known; wires that end beside it: NOR_p7[0], Sum[0], NOR_p7[1], Sum[1], NOR_p7[2], Sum[2], NOR_p7[3], Sum[3], Sum[4], Sum[5], Sum[6], Sum[7], 1'b1
  or or_1 (Sum[0], pulldown_1_out, _74181_1_p3);
  assign pulldown_1_out = ~rot ? A[7] : 1'bz;  // DriverInvSel driverinvsel_1
  // _74181 _74181_1: pin names not known; wires that end beside it: _74151_1_p1, A[0], _74181_1_p3, A[1], Sum[1], A[2], Sum[2], A[3], Sum[3], B[0], B[1], C, B[2], B[3]
  // _7408 AND: pin names not known; wires that end beside it: 1'b0, AND_p2, NOR_p7[0], AND_p4, NOR_p7[1], AND_p6, NOR_p7[2], NOR_p7[3], AND_p2, AND_p4, 1'b0, 1'b0
  PullDown pulldown_2 (.out(N_f));
  assign N_f = ~nALU_Fout ? Sum[7] : 1'bz;  // DriverInvSel driverinvsel_2
  // _74181 _74181_2: pin names not known; wires that end beside it: SEL[0], SEL[1], SEL[2], SEL[3], M, 1'b1, 1'b0, C, A[4], Sum[4], A[5], Sum[5], A[6], Sum[6], A[7], Sum[7], B[4], B[5], _74181_2_p19, B[6], B[7], SEL[0], SEL[1], SEL[2], SEL[3], M, 1'b1, 1'b0
  PullDown pulldown_3 (.out(Z_f));
  assign Z_f = ~nALU_Fout ? AND_p6 : 1'bz;  // DriverInvSel driverinvsel_3
  PullDown pulldown_4 (.out(C_f));
  assign C_f = ~nALU_Fout ? _74181_2_p19 : 1'bz;  // DriverInvSel driverinvsel_4
  PullDown pulldown_5 (.out(V_f));
  assign V_f = ~nALU_Fout ? OVF_p3 : 1'bz;  // DriverInvSel driverinvsel_5
  // _74151 OVF: pin names not known; wires that end beside it: 1'b1, 1'b0, OVF_p3, A[7], Sum[7], B[7], 1'b0, 1'b0, SEL[1], 1'b0, SEL[0], SEL[0], 1'b0, SEL[1], 1'b0, 1'b1, 1'b0

  // Other names for the same wires on the sheet: F7 = Sum[7]; nF_out = nALU_Fout; S[3:0] = SEL
endmodule
