// Digital circuit CPU 16.dig as structural Verilog
module CPU_16 (
  input  Clock,
  input  nWAIT,
  output CLK1,
  output CLK2
);

  wire _74245_1_p13, _74245_1_p14, _74245_1_p15, _74245_1_p16, _74245_1_p17, _74245_1_p18, _74245_1_p19,
       _74245_1_p20, _74245_2_p13, _74245_2_p14, _74245_2_p15, _74245_2_p16, _74245_2_p17, _74245_2_p18,
       _74245_2_p19, _74245_2_p20, _74245_3_p13, _74245_3_p14, _74245_3_p15, _74245_3_p16, _74245_3_p17,
       _74245_3_p18, _74245_3_p19, _74245_3_p20, _74245_4_p13, _74245_4_p14, _74245_4_p15, _74245_4_p16,
       _74245_4_p17, _74245_4_p18, _74245_4_p19, _74245_4_p20, and_1_out, and_2_out, and_3_out, and_4_out,
       and_5_out, and_6_out, and_7_out, and_8_out, and_9_out, and_10_out, and_11_out, and_12_out, and_13_out,
       and_14_out, and_17_out, and_18_out, bussplitter_1_d0, bussplitter_1_d1, bussplitter_1_d2,
       bussplitter_1_d3, bussplitter_1_d4, bussplitter_1_d5, bussplitter_1_d6, bussplitter_1_d7,
       bussplitter_1_d8, bussplitter_1_d9, bussplitter_1_d10, bussplitter_1_d11, bussplitter_1_d12,
       bussplitter_1_d13, bussplitter_1_d14, bussplitter_1_d15, bussplitter_3_d0, bussplitter_3_d1,
       bussplitter_3_d2, bussplitter_3_d3, bussplitter_3_d4, bussplitter_3_d5, bussplitter_3_d6,
       bussplitter_3_d7, bussplitter_3_d8, bussplitter_3_d9, bussplitter_3_d10, bussplitter_3_d11,
       bussplitter_3_d12, bussplitter_3_d13, bussplitter_3_d14, bussplitter_3_d15, COND_C, COND_N, COND_NEG,
       COND_RES, COND_Z, CONV_V, demultiplexer_1_out_0, demultiplexer_1_out_1, demultiplexer_2_out_0,
       demultiplexer_2_out_1, demultiplexer_3_out_0, demultiplexer_3_out_1, demultiplexer_3_out_2,
       demultiplexer_3_out_3, demultiplexer_3_out_4, demultiplexer_3_out_5, demultiplexer_3_out_6,
       demultiplexer_3_out_7, demultiplexer_4_out_0, demultiplexer_4_out_1, demultiplexer_4_out_2,
       demultiplexer_4_out_3, demultiplexer_4_out_4, demultiplexer_4_out_5, demultiplexer_4_out_6,
       demultiplexer_4_out_7, demultiplexer_5_out_1, demultiplexer_5_out_2, demultiplexer_5_out_3,
       demultiplexer_6_out_1, demultiplexer_6_out_2, demultiplexer_6_out_3, demultiplexer_6_out_4,
       demultiplexer_7_out_1, demultiplexer_7_out_2, demultiplexer_7_out_3, demultiplexer_7_out_4,
       demultiplexer_7_out_5, demultiplexer_7_out_6, demultiplexer_7_out_7, demultiplexer_8_out_0,
       demultiplexer_9_out_0, demultiplexer_9_out_1, demultiplexer_10_out_1, demultiplexer_10_out_2,
       demultiplexer_10_out_3, demultiplexer_10_out_4, demultiplexer_10_out_5, demultiplexer_10_out_6,
       demultiplexer_10_out_7, demultiplexer_11_out_0, demultiplexer_11_out_1, demultiplexer_11_out_2,
       demultiplexer_11_out_3, demultiplexer_11_out_4, HLT, HLT_ack, IRQ_0, IRQ_VECT_any, keyboard_1_av,
       MEM_dir, nF_ALUin, nF_DATin, nF_DATout, nF_st, nIO_0, nIO_1, nIO_2, nIO_3, nIO_4, nIO_5, nIO_6, nIO_7,
       nIR_st, nIRQ_ack, nIRQ_en, nMAR_ADSout, nMAR_st, nMDR_DATout, nMDR_st, nMEM_DATout, nMEM_en, nMEM_st,
       nMEM_st2, nOP1_st, nOP2_st, nor_1_out, not_1_out, not_2_out, not_3_out, not_4_out, not_5_out,
       not_6_out, not_8_out, not_9_out, not_10_out, not_25_out, not_26_out, not_27_out, not_28_out,
       not_29_out, not_30_out, not_31_out, not_32_out, not_33_out, not_42_out, not_66_out, not_67_out,
       not_68_out, not_69_out, not_70_out, not_71_out, not_72_out, not_73_out, nPAN_HLTen, nPC_ADSout,
       nPC_DATout, nPC_en, nPC_st, nREG_DATout, nREG_st, nRSH_DATout, nRST, nRST_SEQen, nSEQ_en, nSEQ_st,
       nSEX_DATout, nSP_ADSout, nSP_DATout, nSP_en, nSP_st, nSTAT_st, nSUM_DATout, nSWP_DATout, nWRD_DATout,
       or_1_out, or_4_out, or_5_out, or_6_out, or_7_out, REG_aop, REG_dir, RESET_out, RST_ack, RST_IRen,
       RUN_out, SEQ_val, SP_dir, STP, t_ff_1_nq, t_ff_1_q, TMP_clr, \Σ_Csel , \Σ_Cval , \Σ_M ;
  wire [2:0] AOUT_sel, COND_sel, IRQ_VECT_num, REG_ADS, \µSEQ_out ;
  wire [3:0] alu_1_c_f, DOUT_sel, driverinvsel_4_out, FLAGS, ST_sel, \Σ_sel ;
  wire [4:3] HLT_q;
  wire [6:0] MASK;
  wire [15:0] _15_out, ADDRESS, alu_1_sum, barrelshifter_1_out, bitextender_1_out, d_ff_1_q, d_ff_2_q, DATA,
       driverinvsel_2_out, IR_q, MAR_q, MDR_q, MEMDATA, OP1_q, OP2_q, PC_out, REGS__16x8_d, SP_out;
  wire [47:0] \µCODE_d ;
  wire [47:21] CTRL_q;

  Register #(.Bits(7)) u_MASK (.D(DATA[14:8]), .C(CLK2), .en(~nSTAT_st), .Q(MASK));
  not not_1 (not_1_out, nIO_0);
  Demultiplexer demultiplexer_1 (
    .sel(nMEM_st2), .in(not_1_out), .out_0(demultiplexer_1_out_0), .out_1(demultiplexer_1_out_1));
  not not_2 (not_2_out, demultiplexer_1_out_0);
  not not_3 (not_3_out, demultiplexer_1_out_1);
  not not_4 (not_4_out, not_2_out);
  not not_5 (not_5_out, not_3_out);
  and and_1 (and_1_out, MASK[0], ~IRQ_0);  // And
  and and_2 (and_2_out, MASK[1], ~1'b1);  // And
  and and_3 (and_3_out, MASK[2], ~1'b1);  // And
  and and_4 (and_4_out, MASK[3], ~1'b1);  // And
  and and_5 (and_5_out, MASK[4], ~1'b1);  // And
  and and_6 (and_6_out, MASK[5], ~1'b1);  // And
  and and_7 (and_7_out, MASK[6], ~1'b1);  // And
  Terminal #(.termWidth(80), .termHeight(24)) terminal_1 (.D(DATA[7:0]), .C(CLK2), .en(not_4_out));
  Keyboard keyboard_1 (.C(CLK2), .en(not_5_out), .D(MEMDATA), .av(keyboard_1_av));
  not not_6 (not_6_out, 1'b1);
  not not_7 (IRQ_0, keyboard_1_av);
  PriorityEncoder #(.Selector_Bits(3)) IRQ_VECT (
    .in0(not_6_out), .in1(and_1_out), .in2(and_2_out), .in3(and_3_out), .in4(and_4_out), .in5(and_5_out),
    .in6(and_6_out), .in7(and_7_out), .num(IRQ_VECT_num), .any(IRQ_VECT_any));
  PriorityEncoder #(.Selector_Bits(3)) FAULT_VECT (
    .in0(1'b0), .in1(1'b0), .in2(1'b0), .in3(1'b0), .in4(1'b0), .in5(1'b0), .in6(1'b0), .in7(1'b0));  // open: num, any
  assign DATA = ~or_1_out ? {{13{1'b0}}, IRQ_VECT_num} : 16'bz;  // DriverInvSel driverinvsel_1
  PullDown #(.Bits(16)) pulldown_1 (.out(DATA));
  not not_8 (not_8_out, COND_RES);
  or or_1 (or_1_out, ~IRQ_VECT_any, nIRQ_ack);  // Or
  and and_8 (and_8_out, nSEQ_en, nRST_SEQen);
  and and_9 (and_9_out, nSEQ_st, not_8_out);
  PullUp pullup_1 (.out(HLT));
  nor nor_1 (nor_1_out, HLT, RST_IRen);
  Demultiplexer demultiplexer_2 (
    .sel(ST_sel[3]), .in(1'b1), .out_0(demultiplexer_2_out_0), .out_1(demultiplexer_2_out_1));
  not not_9 (not_9_out, nMEM_en);
  not not_10 (not_10_out, not_32_out);
  assign driverinvsel_2_out = ~RST_IRen ? DATA : 16'bz;  // DriverInvSel driverinvsel_2
  Demultiplexer #(.Selector_Bits(3)) demultiplexer_3 (
    .sel(ADDRESS[15:13]), .in(not_9_out), .out_0(demultiplexer_3_out_0), .out_1(demultiplexer_3_out_1),
    .out_2(demultiplexer_3_out_2), .out_3(demultiplexer_3_out_3), .out_4(demultiplexer_3_out_4),
    .out_5(demultiplexer_3_out_5), .out_6(demultiplexer_3_out_6), .out_7(demultiplexer_3_out_7));
  Demultiplexer #(.Selector_Bits(3)) demultiplexer_4 (
    .sel(ADDRESS[6:4]), .in(not_10_out), .out_0(demultiplexer_4_out_0), .out_1(demultiplexer_4_out_1),
    .out_2(demultiplexer_4_out_2), .out_3(demultiplexer_4_out_3), .out_4(demultiplexer_4_out_4),
    .out_5(demultiplexer_4_out_5), .out_6(demultiplexer_4_out_6), .out_7(demultiplexer_4_out_7));
  CounterPreset #(.Bits(3)) \u_µSEQ  (
    .en(~and_8_out), .C(CLK2), .dir(1'b0), .in({2'b00, SEQ_val}), .ld(~and_9_out), .clr(1'b0),
    .out(\µSEQ_out ));  // open: ovf
  Register u_HLT (.D(nor_1_out), .C(CLK2), .en(~1'b0), .Q(HLT_q[3]));
  Register IRQ (.D(IRQ_VECT_any), .C(CLK2), .en(~nIRQ_en), .Q(HLT_q[4]));
  PullDown #(.Bits(16)) pulldown_2 (.out(driverinvsel_2_out));
  Register #(.Bits(16)) IR (.D(driverinvsel_2_out), .C(CLK2), .en(~nIR_st), .Q(IR_q));
  Demultiplexer #(.Selector_Bits(3)) demultiplexer_5 (
    .sel(AOUT_sel), .in(1'b1), .out_1(demultiplexer_5_out_1), .out_2(demultiplexer_5_out_2),
    .out_3(demultiplexer_5_out_3));  // open: out_0, out_4, out_5, out_6, out_7
  not not_11 (nSP_ADSout, demultiplexer_5_out_1);
  not not_12 (nPC_ADSout, demultiplexer_5_out_2);
  not not_13 (nMAR_ADSout, demultiplexer_5_out_3);
  Demultiplexer #(.Selector_Bits(3)) demultiplexer_6 (
    .sel(COND_sel), .in(1'b1), .out_1(demultiplexer_6_out_1), .out_2(demultiplexer_6_out_2),
    .out_3(demultiplexer_6_out_3), .out_4(demultiplexer_6_out_4));  // open: out_0, out_5, out_6, out_7
  not not_14 (COND_N, demultiplexer_6_out_1);
  not not_15 (COND_Z, demultiplexer_6_out_2);
  not not_16 (CONV_V, demultiplexer_6_out_3);
  not not_17 (COND_C, demultiplexer_6_out_4);
  Demultiplexer #(.Selector_Bits(3)) demultiplexer_7 (
    .sel(ST_sel[2:0]), .in(demultiplexer_2_out_0), .out_1(demultiplexer_7_out_1),
    .out_2(demultiplexer_7_out_2), .out_3(demultiplexer_7_out_3), .out_4(demultiplexer_7_out_4),
    .out_5(demultiplexer_7_out_5), .out_6(demultiplexer_7_out_6), .out_7(demultiplexer_7_out_7));  // open: out_0
  not not_18 (nSP_st, demultiplexer_7_out_1);
  not not_19 (nPC_st, demultiplexer_7_out_2);
  not not_20 (nOP1_st, demultiplexer_7_out_3);
  not not_21 (nOP2_st, demultiplexer_7_out_4);
  not not_22 (nIR_st, demultiplexer_7_out_5);
  not not_23 (nMDR_st, demultiplexer_7_out_6);
  not not_24 (nMEM_st2, demultiplexer_7_out_7);
  Demultiplexer #(.Selector_Bits(3)) demultiplexer_8 (
    .sel(ST_sel[2:0]), .in(demultiplexer_2_out_1), .out_0(demultiplexer_8_out_0));  // open: out_1, out_2, out_3, out_4, out_5, out_6, out_7
  not not_25 (not_25_out, demultiplexer_8_out_0);
  not not_26 (not_26_out, demultiplexer_3_out_0);
  not not_27 (not_27_out, demultiplexer_3_out_1);
  not not_28 (not_28_out, demultiplexer_3_out_2);
  not not_29 (not_29_out, demultiplexer_3_out_3);
  not not_30 (not_30_out, demultiplexer_3_out_4);
  not not_31 (not_31_out, demultiplexer_3_out_5);
  not not_32 (not_32_out, demultiplexer_3_out_6);
  not not_33 (not_33_out, demultiplexer_3_out_7);
  not not_34 (nIO_0, demultiplexer_4_out_0);
  not not_35 (nIO_1, demultiplexer_4_out_1);
  not not_36 (nIO_2, demultiplexer_4_out_2);
  not not_37 (nIO_3, demultiplexer_4_out_3);
  not not_38 (nIO_4, demultiplexer_4_out_4);
  not not_39 (nIO_5, demultiplexer_4_out_5);
  not not_40 (nIO_6, demultiplexer_4_out_6);
  not not_41 (nIO_7, demultiplexer_4_out_7);
  and and_10 (and_10_out, not_26_out, not_27_out, not_28_out, not_29_out, not_30_out, not_31_out);
  // Probe on IR_q[15:6]
  Multiplexer #(.Bits(3)) multiplexer_1 (.sel(REG_aop), .in_0(IR_q[5:3]), .in_1(IR_q[2:0]), .out(REG_ADS));
  or or_2 (nMEM_st, ~CLK2, nMEM_st2);  // Or
  or or_3 (nREG_st, ~CLK2, not_25_out);  // Or
  ROM #(.AddrBits(15), .Bits(48)) \u_µCODE  (.A({IR_q[15:6], HLT_q, \µSEQ_out }), .sel(1'b1), .D(\µCODE_d ));
  or or_4 (or_4_out, ~nMEM_st2, not_33_out);  // Or
  and and_11 (and_11_out, ~COND_N, FLAGS[0]);  // And
  ROM #(.AddrBits(16), .Bits(16)) ROM_16x64k (.A(ADDRESS), .sel(not_42_out), .D(MEMDATA));
  not not_42 (not_42_out, or_4_out);
  RAMSinglePortSel #(.AddrBits(16), .Bits(16)) RAM0_16x64k (
    .A(ADDRESS), .CS(~and_10_out), .WE(~nMEM_st), .OE(~nMEM_DATout), .D(MEMDATA));
  and and_12 (and_12_out, ~COND_Z, FLAGS[1]);  // And
  D_FF #(.Bits(48)) CTRL (
    .D(\µCODE_d ), .C(CLK1),
    .Q({CTRL_q[47:38], RST_ack, CTRL_q[36], HLT_ack, TMP_clr, REG_aop, REG_dir, CTRL_q[31], nF_ALUin, COND_NEG, MEM_dir, CTRL_q[27:26], SP_dir, CTRL_q[24], SEQ_val, CTRL_q[22:21], \Σ_Cval , \Σ_Csel , \Σ_M , \Σ_sel , COND_sel, AOUT_sel, DOUT_sel, ST_sel}));  // open: nQ
  and and_13 (and_13_out, ~CONV_V, FLAGS[2]);  // And
  Demultiplexer demultiplexer_9 (
    .sel(DOUT_sel[3]), .in(1'b1), .out_0(demultiplexer_9_out_0), .out_1(demultiplexer_9_out_1));
  BusSplitter #(.Bits(16)) bussplitter_1 (
    .D(MEMDATA), .OE(MEM_dir), .D0(bussplitter_1_d0), .D1(bussplitter_1_d1), .D2(bussplitter_1_d2),
    .D3(bussplitter_1_d3), .D4(bussplitter_1_d4), .D5(bussplitter_1_d5), .D6(bussplitter_1_d6),
    .D7(bussplitter_1_d7), .D8(bussplitter_1_d8), .D9(bussplitter_1_d9), .D10(bussplitter_1_d10),
    .D11(bussplitter_1_d11), .D12(bussplitter_1_d12), .D13(bussplitter_1_d13), .D14(bussplitter_1_d14),
    .D15(bussplitter_1_d15));
  PullDown #(.Bits(16)) pulldown_3 (.out(MEMDATA));
  or or_5 (or_5_out, and_11_out, and_12_out);
  and and_14 (and_14_out, ~COND_C, ~FLAGS[3]);  // And
  PullDown pulldown_4 (.out(bussplitter_1_d0));
  PullDown pulldown_5 (.out(bussplitter_1_d1));
  PullDown pulldown_6 (.out(bussplitter_1_d2));
  PullDown pulldown_7 (.out(bussplitter_1_d15));
  PullDown pulldown_8 (.out(bussplitter_1_d14));
  PullDown pulldown_9 (.out(bussplitter_1_d13));
  not not_43 (nSEQ_en, CTRL_q[21]);
  not not_44 (nSEQ_st, CTRL_q[22]);
  not not_45 (nPC_en, CTRL_q[24]);
  not not_46 (nSP_en, CTRL_q[26]);
  not not_47 (nMEM_en, CTRL_q[27]);
  not not_48 (nIRQ_en, CTRL_q[31]);
  not not_49 (nMAR_st, CTRL_q[38]);
  not not_50 (nF_st, CTRL_q[39]);
  not not_51 (nSTAT_st, CTRL_q[40]);
  or or_6 (or_6_out, and_13_out, and_14_out);
  Demultiplexer #(.Selector_Bits(3)) demultiplexer_10 (
    .sel(DOUT_sel[2:0]), .in(demultiplexer_9_out_0), .out_1(demultiplexer_10_out_1),
    .out_2(demultiplexer_10_out_2), .out_3(demultiplexer_10_out_3), .out_4(demultiplexer_10_out_4),
    .out_5(demultiplexer_10_out_5), .out_6(demultiplexer_10_out_6), .out_7(demultiplexer_10_out_7));  // open: out_0
  not not_52 (nF_DATout, demultiplexer_10_out_1);
  not not_53 (nSP_DATout, demultiplexer_10_out_2);
  not not_54 (nPC_DATout, demultiplexer_10_out_3);
  not not_55 (nSUM_DATout, demultiplexer_10_out_4);
  not not_56 (nRSH_DATout, demultiplexer_10_out_5);
  not not_57 (nSEX_DATout, demultiplexer_10_out_6);
  not not_58 (nSWP_DATout, demultiplexer_10_out_7);
  Demultiplexer #(.Selector_Bits(3)) demultiplexer_11 (
    .sel(DOUT_sel[2:0]), .in(demultiplexer_9_out_1), .out_0(demultiplexer_11_out_0),
    .out_1(demultiplexer_11_out_1), .out_2(demultiplexer_11_out_2), .out_3(demultiplexer_11_out_3),
    .out_4(demultiplexer_11_out_4));  // open: out_5, out_6, out_7
  not not_59 (nWRD_DATout, demultiplexer_11_out_0);
  not not_60 (nMDR_DATout, demultiplexer_11_out_1);
  not not_61 (nMEM_DATout, demultiplexer_11_out_2);
  not not_62 (nREG_DATout, demultiplexer_11_out_3);
  not not_63 (nIRQ_ack, demultiplexer_11_out_4);
  PullDown pulldown_10 (.out(bussplitter_1_d3));
  PullDown pulldown_11 (.out(bussplitter_1_d4));
  PullDown pulldown_12 (.out(bussplitter_1_d5));
  PullDown pulldown_13 (.out(bussplitter_1_d6));
  PullDown pulldown_14 (.out(bussplitter_1_d12));
  PullDown pulldown_15 (.out(bussplitter_1_d11));
  PullDown pulldown_16 (.out(bussplitter_1_d10));
  PullDown pulldown_17 (.out(bussplitter_1_d9));
  not not_64 (nF_DATin, nF_ALUin);
  PullDown pulldown_18 (.out(bussplitter_1_d7));
  PullDown pulldown_19 (.out(bussplitter_1_d8));
  or or_7 (or_7_out, or_5_out, or_6_out);
  // _74245 _74245_1: pin names not known; wires that end beside it: MEM_dir, 1'b1, 1'b0, bussplitter_1_d0, bussplitter_1_d1, bussplitter_1_d2, bussplitter_1_d3, bussplitter_1_d4, bussplitter_1_d5, bussplitter_1_d6, bussplitter_1_d7, 1'b0, _74245_1_p13, _74245_1_p14, _74245_1_p15, _74245_1_p16, _74245_1_p17, _74245_1_p18, _74245_1_p19, _74245_1_p20
  // _74245 _74245_2: pin names not known; wires that end beside it: MEM_dir, 1'b1, 1'b0, bussplitter_1_d8, bussplitter_1_d9, bussplitter_1_d10, bussplitter_1_d11, bussplitter_1_d12, bussplitter_1_d13, bussplitter_1_d14, bussplitter_1_d15, 1'b0, _74245_2_p13, _74245_2_p14, _74245_2_p15, _74245_2_p16, _74245_2_p17, _74245_2_p18, _74245_2_p19, _74245_2_p20
  PullDown pulldown_20 (.out(Clock));
  not not_65 (nRST, RESET_out);
  DipSwitch RESET (.out(RESET_out));
  T_FF #(.withEnable("false")) t_ff_1 (.C(not_66_out), .Q(t_ff_1_q), .nQ(t_ff_1_nq));
  not not_66 (not_66_out, Clock);
  not not_67 (not_67_out, or_7_out);
  PullDown pulldown_21 (.out(_74245_2_p20));
  PullDown pulldown_22 (.out(_74245_2_p19));
  PullDown pulldown_23 (.out(_74245_2_p18));
  not not_68 (not_68_out, TMP_clr);
  not not_69 (not_69_out, RST_ack);
  Multiplexer multiplexer_2 (.sel(COND_NEG), .in_0(or_7_out), .in_1(not_67_out), .out(COND_RES));
  PullDown pulldown_24 (.out(_74245_2_p17));
  PullDown pulldown_25 (.out(_74245_2_p16));
  PullDown pulldown_26 (.out(_74245_2_p15));
  PullDown pulldown_27 (.out(_74245_2_p14));
  and and_15 (CLK1, Clock, t_ff_1_q);
  and and_16 (CLK2, t_ff_1_nq, ~nWAIT, Clock);  // And
  // _7474 _7474_1: pin names not known; wires that end beside it: nRST, 1'b0, 1'b0, not_68_out, nRST, 1'b0, 1'b0, not_69_out, 1'b1, 1'b0, nRST_SEQen, RST_IRen
  assign DATA = ~nWRD_DATout ? {16{1'b1}} : 16'bz;  // DriverInvSel driverinvsel_3
  PullDown pulldown_28 (.out(_74245_2_p13));
  PullDown pulldown_29 (.out(_74245_1_p20));
  PullDown pulldown_30 (.out(_74245_1_p19));
  PullDown pulldown_31 (.out(_74245_1_p18));
  PullDown pulldown_32 (.out(_74245_1_p17));
  PullDown pulldown_33 (.out(_74245_1_p16));
  PullDown pulldown_34 (.out(_74245_1_p15));
  PullDown pulldown_35 (.out(_74245_1_p14));
  PullDown #(.Bits(16)) pulldown_36 (.out(DATA));
  not not_70 (not_70_out, MEM_dir);
  BusSplitter #(.Bits(16)) bussplitter_2 (
    .D(DATA), .OE(not_70_out), .D0(_74245_1_p13), .D1(_74245_1_p14), .D2(_74245_1_p15), .D3(_74245_1_p16),
    .D4(_74245_1_p17), .D5(_74245_1_p18), .D6(_74245_1_p19), .D7(_74245_1_p20), .D8(_74245_2_p13),
    .D9(_74245_2_p14), .D10(_74245_2_p15), .D11(_74245_2_p16), .D12(_74245_2_p17), .D13(_74245_2_p18),
    .D14(_74245_2_p19), .D15(_74245_2_p20));
  PullDown pulldown_37 (.out(_74245_1_p13));
  LED D15 (.in(d_ff_1_q[15]));
  LED A15 (.in(d_ff_2_q[15]));
  DipSwitch _15 (.out(_15_out[15]));
  RAMSinglePortSel #(.AddrBits(3), .Bits(16)) REGS__16x8 (
    .A(REG_ADS), .CS(~1'b0), .WE(~nREG_st), .OE(~nREG_DATout), .D(REGS__16x8_d));
  LED D13 (.in(d_ff_1_q[13]));
  LED D14 (.in(d_ff_1_q[14]));
  LED A13 (.in(d_ff_2_q[13]));
  LED A14 (.in(d_ff_2_q[14]));
  DipSwitch _13 (.out(_15_out[13]));
  DipSwitch _14 (.out(_15_out[14]));
  Register #(.Bits(16)) OP1 (.D(DATA), .C(CLK2), .en(~nOP1_st), .Q(OP1_q));
  Register #(.Bits(16)) OP2 (.D(DATA), .C(CLK2), .en(~nOP2_st), .Q(OP2_q));
  LED D12 (.in(d_ff_1_q[12]));
  LED A12 (.in(d_ff_2_q[12]));
  DipSwitch _12 (.out(_15_out[12]));
  BusSplitter #(.Bits(16)) bussplitter_3 (
    .D(REGS__16x8_d), .OE(REG_dir), .D0(bussplitter_3_d0), .D1(bussplitter_3_d1), .D2(bussplitter_3_d2),
    .D3(bussplitter_3_d3), .D4(bussplitter_3_d4), .D5(bussplitter_3_d5), .D6(bussplitter_3_d6),
    .D7(bussplitter_3_d7), .D8(bussplitter_3_d8), .D9(bussplitter_3_d9), .D10(bussplitter_3_d10),
    .D11(bussplitter_3_d11), .D12(bussplitter_3_d12), .D13(bussplitter_3_d13), .D14(bussplitter_3_d14),
    .D15(bussplitter_3_d15));
  PullDown #(.Bits(16)) pulldown_38 (.out(REGS__16x8_d));
  LED D11 (.in(d_ff_1_q[11]));
  LED A11 (.in(d_ff_2_q[11]));
  DipSwitch _11 (.out(_15_out[11]));
  PullDown pulldown_39 (.out(bussplitter_3_d0));
  PullDown pulldown_40 (.out(bussplitter_3_d1));
  PullDown pulldown_41 (.out(bussplitter_3_d2));
  PullDown pulldown_42 (.out(bussplitter_3_d15));
  PullDown pulldown_43 (.out(bussplitter_3_d14));
  PullDown pulldown_44 (.out(bussplitter_3_d13));
  LED D9 (.in(d_ff_1_q[9]));
  LED D10 (.in(d_ff_1_q[10]));
  LED A9 (.in(d_ff_2_q[9]));
  LED A10 (.in(d_ff_2_q[10]));
  DipSwitch _9 (.out(_15_out[9]));
  DipSwitch _10 (.out(_15_out[10]));
  PullDown pulldown_45 (.out(bussplitter_3_d3));
  PullDown pulldown_46 (.out(bussplitter_3_d4));
  PullDown pulldown_47 (.out(bussplitter_3_d5));
  PullDown pulldown_48 (.out(bussplitter_3_d6));
  PullDown pulldown_49 (.out(bussplitter_3_d12));
  PullDown pulldown_50 (.out(bussplitter_3_d11));
  PullDown pulldown_51 (.out(bussplitter_3_d10));
  PullDown pulldown_52 (.out(bussplitter_3_d9));
  LED D8 (.in(d_ff_1_q[8]));
  LED A8 (.in(d_ff_2_q[8]));
  DipSwitch _8 (.out(_15_out[8]));
  BarrelShifter #(.Bits(16), .direction("right")) barrelshifter_1 (
    .in(OP1_q), .shift(5'b00001), .out(barrelshifter_1_out));
  BitExtender bitextender_1 (.in(OP1_q[7:0]), .out(bitextender_1_out));
  PullDown pulldown_53 (.out(bussplitter_3_d7));
  PullDown pulldown_54 (.out(bussplitter_3_d8));
  LED D7 (.in(d_ff_1_q[7]));
  LED A7 (.in(d_ff_2_q[7]));
  DipSwitch _7 (.out(_15_out[7]));
  ALU alu_1 (
    .Sum(alu_1_sum), .C_sel(\Σ_Csel ), .C_val(\Σ_Cval ), .nCin(FLAGS[3]), .A(OP1_q), .Sel(\Σ_sel ),
    .B(OP2_q), .M(\Σ_M ), .C_f(alu_1_c_f[3]), .N_f(alu_1_c_f[2]), .Z_f(alu_1_c_f[1]), .V_f(alu_1_c_f[0]));
  // _74245 _74245_3: pin names not known; wires that end beside it: REG_dir, 1'b1, 1'b0, bussplitter_3_d0, bussplitter_3_d1, bussplitter_3_d2, bussplitter_3_d3, bussplitter_3_d4, bussplitter_3_d5, bussplitter_3_d6, bussplitter_3_d7, 1'b0, _74245_3_p13, _74245_3_p14, _74245_3_p15, _74245_3_p16, _74245_3_p17, _74245_3_p18, _74245_3_p19, _74245_3_p20
  // _74245 _74245_4: pin names not known; wires that end beside it: REG_dir, 1'b1, 1'b0, bussplitter_3_d8, bussplitter_3_d9, bussplitter_3_d10, bussplitter_3_d11, bussplitter_3_d12, bussplitter_3_d13, bussplitter_3_d14, bussplitter_3_d15, 1'b0, _74245_4_p13, _74245_4_p14, _74245_4_p15, _74245_4_p16, _74245_4_p17, _74245_4_p18, _74245_4_p19, _74245_4_p20
  LED D5 (.in(d_ff_1_q[5]));
  LED D6 (.in(d_ff_1_q[6]));
  LED A5 (.in(d_ff_2_q[5]));
  LED A6 (.in(d_ff_2_q[6]));
  DipSwitch _5 (.out(_15_out[5]));
  DipSwitch _6 (.out(_15_out[6]));
  assign driverinvsel_4_out = ~nF_DATin ? DATA[3:0] : 4'bz;  // DriverInvSel driverinvsel_4
  LED D4 (.in(d_ff_1_q[4]));
  LED A4 (.in(d_ff_2_q[4]));
  DipSwitch _4 (.out(_15_out[4]));
  assign driverinvsel_4_out = ~nF_ALUin ? alu_1_c_f : 4'bz;  // DriverInvSel driverinvsel_5
  assign DATA = ~nRSH_DATout ? barrelshifter_1_out : 16'bz;  // DriverInvSel driverinvsel_6
  assign DATA = ~nSEX_DATout ? bitextender_1_out : 16'bz;  // DriverInvSel driverinvsel_7
  assign DATA = ~nSWP_DATout ? {OP1_q[7:0], OP1_q[15:8]} : 16'bz;  // DriverInvSel driverinvsel_8
  PullDown pulldown_55 (.out(_74245_4_p20));
  PullDown pulldown_56 (.out(_74245_4_p19));
  PullDown pulldown_57 (.out(_74245_4_p18));
  LED D3 (.in(d_ff_1_q[3]));
  and and_17 (and_17_out, CLK2, ~HLT_ack);  // And
  LED A3 (.in(d_ff_2_q[3]));
  and and_18 (and_18_out, CLK2, ~HLT_ack);  // And
  DipSwitch _3 (.out(_15_out[3]));
  PullDown #(.Bits(4)) pulldown_58 (.out(driverinvsel_4_out));
  PullDown #(.Bits(16)) pulldown_59 (.out(DATA));
  PullDown #(.Bits(16)) pulldown_60 (.out(DATA));
  PullDown #(.Bits(16)) pulldown_61 (.out(DATA));
  PullDown pulldown_62 (.out(_74245_4_p17));
  PullDown pulldown_63 (.out(_74245_4_p16));
  PullDown pulldown_64 (.out(_74245_4_p15));
  PullDown pulldown_65 (.out(_74245_4_p14));
  LED D1 (.in(d_ff_1_q[1]));
  LED D2 (.in(d_ff_1_q[2]));
  D_FF #(.Bits(16)) d_ff_1 (.D(DATA), .C(and_17_out), .Q(d_ff_1_q));  // open: nQ
  LED A1 (.in(d_ff_2_q[1]));
  LED A2 (.in(d_ff_2_q[2]));
  D_FF #(.Bits(16)) d_ff_2 (.D(ADDRESS), .C(and_18_out), .Q(d_ff_2_q));  // open: nQ
  DipSwitch _1 (.out(_15_out[1]));
  DipSwitch _2 (.out(_15_out[2]));
  Register #(.Bits(4)) F__NZVC (.D(driverinvsel_4_out), .C(CLK2), .en(~nF_st), .Q(FLAGS));
  PullDown pulldown_66 (.out(_74245_4_p13));
  PullDown pulldown_67 (.out(_74245_3_p20));
  PullDown pulldown_68 (.out(_74245_3_p19));
  PullDown pulldown_69 (.out(_74245_3_p18));
  LED D0 (.in(d_ff_1_q[0]));
  LED A0 (.in(d_ff_2_q[0]));
  assign DATA = ~1'b1 ? _15_out : 16'bz;  // DriverInvSel driverinvsel_9
  DipSwitch _0 (.out(_15_out[0]));
  PullDown pulldown_70 (.out(_74245_3_p17));
  PullDown pulldown_71 (.out(_74245_3_p16));
  PullDown pulldown_72 (.out(_74245_3_p15));
  PullDown pulldown_73 (.out(_74245_3_p14));
  not not_71 (not_71_out, REG_dir);
  BusSplitter #(.Bits(16)) bussplitter_4 (
    .D(DATA), .OE(not_71_out), .D0(_74245_3_p13), .D1(_74245_3_p14), .D2(_74245_3_p15), .D3(_74245_3_p16),
    .D4(_74245_3_p17), .D5(_74245_3_p18), .D6(_74245_3_p19), .D7(_74245_3_p20), .D8(_74245_4_p13),
    .D9(_74245_4_p14), .D10(_74245_4_p15), .D11(_74245_4_p16), .D12(_74245_4_p17), .D13(_74245_4_p18),
    .D14(_74245_4_p19), .D15(_74245_4_p20));
  PullDown pulldown_74 (.out(_74245_3_p13));
  LED V (.in(FLAGS[2]));
  LED C (.in(not_72_out));
  not not_72 (not_72_out, FLAGS[3]);
  assign HLT = ~nPAN_HLTen ? RUN_out : 1'bz;  // DriverInvSel driverinvsel_10
  DipSwitch #(.dipDefault("true")) RUN (.out(RUN_out));
  assign DATA = ~nSUM_DATout ? alu_1_sum : 16'bz;  // DriverInvSel driverinvsel_11
  PullDown #(.Bits(16)) pulldown_75 (.out(DATA));
  assign DATA = ~nF_DATout ? {1'b0, MASK, 4'b0000, FLAGS} : 16'bz;  // DriverInvSel driverinvsel_12
  PullDown #(.Bits(16)) pulldown_76 (.out(DATA));
  LED Z (.in(FLAGS[1]));
  DipSwitch STEP (.out(STP));
  LED N (.in(FLAGS[0]));
  CounterPreset #(.Bits(16)) PC (
    .en(~nPC_en), .C(CLK2), .dir(1'b0), .in(DATA), .ld(~nPC_st), .clr(1'b0), .out(PC_out));  // open: ovf
  CounterPreset #(.Bits(16)) SP (
    .en(~nSP_en), .C(CLK2), .dir(SP_dir), .in(DATA), .ld(~nSP_st), .clr(1'b0), .out(SP_out));  // open: ovf
  assign ADDRESS = ~nPC_ADSout ? PC_out : 16'bz;  // DriverInvSel driverinvsel_13
  assign ADDRESS = ~nSP_ADSout ? SP_out : 16'bz;  // DriverInvSel driverinvsel_14
  assign DATA = ~nPC_DATout ? PC_out : 16'bz;  // DriverInvSel driverinvsel_15
  PullDown #(.Bits(16)) pulldown_77 (.out(DATA));
  PullDown #(.Bits(16)) pulldown_78 (.out(ADDRESS));
  assign DATA = ~nSP_DATout ? SP_out : 16'bz;  // DriverInvSel driverinvsel_16
  PullDown #(.Bits(16)) pulldown_79 (.out(DATA));
  PullDown #(.Bits(16)) pulldown_80 (.out(ADDRESS));
  not not_73 (not_73_out, STP);
  Register #(.Bits(16)) MDR (.D(DATA), .C(CLK2), .en(~nMDR_st), .Q(MDR_q));
  Register #(.Bits(16)) MAR (.D(DATA), .C(CLK2), .en(~nMAR_st), .Q(MAR_q));
  // _7474 _7474_2: pin names not known; wires that end beside it: not_73_out, 1'b0, 1'b0, HLT_ack, 1'b0, 1'b0, 1'b0, 1'b0, 1'b1, 1'b0, nPAN_HLTen
  assign DATA = ~nMDR_DATout ? MDR_q : 16'bz;  // DriverInvSel driverinvsel_17
  assign ADDRESS = ~nMAR_ADSout ? MAR_q : 16'bz;  // DriverInvSel driverinvsel_18
  PullDown #(.Bits(16)) pulldown_81 (.out(DATA));
  PullDown #(.Bits(16)) pulldown_82 (.out(ADDRESS));

  // Other names for the same wires on the sheet: CLK_1 = CLK1; CLK_2 = CLK2

  // Notes on the sheet:
  //   Clock: Hz: 2147483647
  //   Control Sequencing
  //   Control Decoding
  //   Memory/IRQ
  //   contents of µCODE (hex, n*v repeats v):
  //   4982002a5,18000200000,4000200080,20184003a2,4*0,8*880000000,4982002a5
  //   ,40062000c0,200036,8200117,1e2003a2,8200197,10000400000,0,8*880000000
  //   ,4982002a5,880000000,6*0,8*880000000,4982002a5,40062000c0,200036
  //   ,8200117,1e2003a2,8200197,10000400000,0,8*880000000,4982002a5
  //   ,1200000,6*0,24*880000000,4982002a5,1200000,6*0,24*880000000,4982002a5
  //   ,1200000,6*0,8*880000000,4982002a5,40062000c0,200036,8200117,1e2003a2
  //   ,8200197,10000400000,0,8*880000000,4982002a5,182001a2,4200000
  //   ,180582001a0,49cc002a5,0,0,0,8*880000000,4982002a5,40062000c0
  //   ,200036,8200117,1e2003a2,8200197,10000400000,0,8*880000000,4982002a5
  //   ,1200000,6*0,8*880000000,4982002a5,40062000c0,200036,8200117,1e2003a2
  //   ,8200197,10000400000,0,8*880000000,4982002a5,1200000,6*0,8*880000000
  //   ,4982002a5,40062000c0,200036,8200117,1e2003a2,8200197,10000400000
  //   ,0,8*880000000,4982002a5,83414000b0,6*0,8*880000000,4982002a5
  //   ,40062000c0,200036,8200117,1e2003a2,8200197,10000400000,0,8*880000000
  //   ,4982002a5,103414000b0,6*0,8*880000000,4982002a5,40062000c0,200036
  //   ,8200117,1e2003a2,8200197,10000400000,0,8*880000000,4982002a5
  //   ,201400018,6*0,8*880000000,4982002a5,40062000c0,200036,8200117
  //   ,1e2003a2,8200197,10000400000,0,8*880000000,4982002a5,1200000
  //   ,6*0,8*880000000,4982002a5,40062000c0,200036,8200117,1e2003a2
  //   ,8200197,10000400000,0,8*880000000,4982002a5,1200000,6*0,8*880000000
  //   ,4982002a5,40062000c0,200036,8200117,1e2003a2,8200197,10000400000
  //   ,0,8*880000000,4982002a5,1200000,6*0,8*880000000,4982002a5,40062000c0
  //   ,200036,8200117,1e2003a2,8200197,10000400000,0,8*880000000,4982002a5
  //   ,7200000,3082001b7,200200028,182002a4,1200023,524041,0,8*880000000
  //   ,4982002a5,40062000c0,200036,8200117,1e2003a2,8200197,10000400000
  //   ,0,8*880000000,4982002a5,3012000b1,2182001a8,49c4002a5,4*0,8*880000000
  //   ,4982002a5,40062000c0,200036,8200117,1e2003a2,8200197,10000400000
  //   ,0,8*880000000,4982002a5,1200000,6*0,8*880000000,4982002a5,40062000c0
  //   ,200036,8200117,1e2003a2,8200197,10000400000,0,8*880000000,4982002a5
  //   ,1200000,182002a6,400092,4*0,8*880000000,4982002a5,40062000c0
  //   ,200036,8200117,1e2003a2,8200197,10000400000,0,8*880000000,4982002a5
  //   ,1200000,6*0,8*880000000,4982002a5,40062000c0,200036,8200117,1e2003a2
  //   ,8200197,10000400000,0,8*880000000,4982002a5,1200000,6*0,8*880000000
  //   ,4982002a5,40062000c0,200036,8200117,1e2003a2,8200197,10000400000
  //   ,0,8*880000000,4982002a5,1200000,6*0,8*880000000,4982002a5,40062000c0
  //   ,200036,8200117,1e2003a2,8200197,10000400000,0,8*880000000,4982002a5
  //   ,1200000,6*0,8*880000000,4982002a5,40062000c0,200036,8200117,1e2003a2
  //   ,8200197,10000400000,0,8*880000000,4982002a5,1200000,6*0,8*880000000
  //   ,4982002a5,40062000c0,200036,8200117,1e2003a2,8200197,10000400000
  //   ,0,8*880000000,4982002a5,1200000,6*0,8*880000000,4982002a5,40062000c0
  //   ,200036,8200117,1e2003a2,8200197,10000400000,0,8*880000000,4982002a5
  //   ,1200000,6*0,8*880000000,4982002a5,40062000c0,200036,8200117,1e2003a2
  //   ,8200197,10000400000,0,8*880000000,4982002a5,7200000,182002a6
  //   ,9200117,6200000,8200137,400092,0,8*880000000,4982002a5,40062000c0
  //   ,200036,8200117,1e2003a2,8200197,10000400000,0,8*880000000,4982002a5
  //   ,1200000,6*0,8*880000000,4982002a5,40062000c0,200036,8200117,1e2003a2
  //   ,8200197,10000400000,0,8*880000000,4982002a5,1200000,6*0,8*880000000
  //   ,4982002a5,40062000c0,200036,8200117,1e2003a2,8200197,10000400000
  //   ,0,8*880000000,4982002a5,1200000,6*0,8*880000000,4982002a5,40062000c0
  //   ,200036,8200117,1e2003a2,8200197,10000400000,0,8*880000000,4982002a5
  //   ,1200000,6*0,8*880000000,4982002a5,40062000c0,200036,8200117,1e2003a2
  //   ,8200197,10000400000,0,8*880000000,4982002a5,1200000,6*0,8*880000000
  //   ,4982002a5,40062000c0,200036,8200117,1e2003a2,8200197,10000400000
  //   ,0,8*880000000,4982002a5,1200000,6*0,8*880000000,4982002a5,40062000c0
  //   ,200036,8200117,1e2003a2,8200197,10000400000,0,8*880000000,4982002a5
  //   ,1200000,6*0,8*880000000,4982002a5,40062000c0,200036,8200117,1e2003a2
  //   ,8200197,10000400000,0,8*880000000,4982002a5,1200000,200033,182002a4
  //   ,21201000,524042,0,0,8*880000000,4982002a5,40062000c0,200036,8200117
  //   ,1e2003a2,8200197,10000400000,0,8*880000000,4982002a5,1200000
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  //   contents of ROM_16x64k (hex, n*v repeats v):
  //   57344*0,39c0,c000,1e40,f073,1,387,0,31c0,fd00,640,f06a,3c7,d40
  //   ,100,1e40,3e,c000,1e01,0,1e40,200,1fe,1e40,200,1ff,b240,1fe,1ff
  //   ,840,fffc,3001,640,f081,3201,be00,1f,8c0,15,be00,a,840,16,be00
  //   ,8,940,ffec,be01,0,940,3,440,e019,dc01,1e40,8,c000,440,e019,1040
  //   ,c000,da01,440,e019,d00,4000,1040,c000,1200,1ff,dc00,1ec0,0,387
  //   ,0,31c0,200,640,f090,3c7,387,0,31c0,fd52,640,f06a,3c7,440,e00c
  //   ,4008*0,3004,3007,1e04,0,102f,640,f035,1e40,3a,c000,1e40,20,c000
  //   ,3005,162f,640,f035,1e40,20,c000,da04,da05,be04,8,940,fff5,1e40
  //   ,20,c000,3205,1e04,0,162f,640,f05a,1e40,20,c000,da04,da05,be04
  //   ,8,940,fff5,1e40,a,c000,b02e,940,ffd1,3204,3207,40,3006,103e,3c06
  //   ,4*d806,8e06,f,1870,fd60,c000,103e,3c06,8e06,f,1870,fd60,c000
  //   ,103e,4*d806,8e06,f,1870,fd60,c000,103e,8e06,f,1870,fd60,c000
  //   ,3206,140,3006,103e,3c06,8e06,ff,1870,fd71,c000,103e,8e06,ff,1870
  //   ,fd71,c000,3206,140,1838,ffff,1a40,c000,bec0,0,940,fffb,140,1200
  //   ,1fe,12c0,c000,da00,be00,2ff,940,3,1e00,200,1040,1fe,140,d00,4000
  //   ,1201,1ff,1608,da01,be01,2ff,940,3,1e01,200,1048,1ff,140,3002
  //   ,1838,ffff,1839,ffff,1602,be02,1f,8c0,b,be02,0,840,b,be02,8,840
  //   ,b,440,f0a8,1151,da00,440,f095,1ec1,0,3202,140,b839,ffff,840,fff6
  //   ,dc01,440,f0a5,3149*0,41,54,4c,41,53,20,4d,61,63,68,69,6e,65,20
  //   ,43,6f,64,65,20,4d,6f,6e,69,74,6f,72,20,31,36,a,28,63,29,32,30
  //   ,32,31,20,41,54,4c,41,53,20,44,69,67,69,74,61,6c,20,53,79,73,74
  //   ,65,6d,73,2c,20,48,61,79,64,65,6e,20,42,75,73,63,68,65,72,a,a
  //   ,0,3e,3e,20,0,53,79,6e,74,61,78,20,65,72,72,6f,72,a,0,30,31,32
  //   ,33,34,35,36,37,38,39,41,42,43,44,45,46,0,32*2e,20,21,22,23,24
  //   ,25,26,27,28,29,2a,2b,2c,2d,2e,2f,30,31,32,33,34,35,36,37,38,39
  //   ,3a,3b,3c,3d,3e,3f,40,41,42,43,44,45,46,47,48,49,4a,4b,4c,4d,4e
  //   ,4f,50,51,52,53,54,55,56,57,58,59,5a,5b,5c,5d,5e,5f,60,61,62,63
  //   ,64,65,66,67,68,69,6a,6b,6c,6d,6e,6f,70,71,72,73,74,75,76,77,78
  //   ,79,7a,7b,7c,7d,7e,129*2e,398*0,e000
  //   ALU
  //   Registers
  //   Control Panel
  //   ATLAS CPU-16
  //   By Hayden B.
endmodule
