// Digital circuit CPU 8.dig as structural Verilog
module CPU_8 (
  input  [7:0] DAT,
  input  [7:0] ADDlo,
  input  [7:0] ADDhi,
  input  Clock,
  input  pcd,
  input  RST,
  input  NMI,
  input  IRJ,
  input  IRK,
  input  DMA,
  input  nWAIT,
  input  [2:0] Csel,
  input  [4:0] Bsel,
  input  [4:0] Rsel,
  input  [2:0] Asel,
  input  [3:0] Fsel,
  input  [2:0] Zsel,
  input  HALT,
  output CLK1,
  output CLK2
);

  wire A_clr, add_1_c_o, alu_1_p13, alu_1_p14, and_1_out, and_2_out, and_3_out, and_4_out, and_5_out,
       and_6_out, and_7_out, and_8_out, and_9_out, and_10_out, and_11_out, and_12_out, BCD_clr, BRK_Vout,
       comparator_1_eq, comparator_2_eq, COND_C, COND_N, COND_P, COND_RES, COND_X, COND_Y, COND_Z, CONV_V,
       D1, D2, D3, D4, D5, D6, demultiplexer_1_out_1, demultiplexer_1_out_2, demultiplexer_1_out_3,
       demultiplexer_2_out_1, demultiplexer_2_out_2, demultiplexer_2_out_3, demultiplexer_2_out_4,
       demultiplexer_2_out_5, demultiplexer_2_out_6, demultiplexer_2_out_7, demultiplexer_3_out_1,
       demultiplexer_3_out_2, demultiplexer_3_out_3, demultiplexer_3_out_4, demultiplexer_3_out_5,
       demultiplexer_3_out_6, demultiplexer_4_out_1, demultiplexer_4_out_2, demultiplexer_4_out_3,
       demultiplexer_4_out_4, demultiplexer_4_out_5, demultiplexer_4_out_6, demultiplexer_4_out_7,
       demultiplexer_4_out_8, demultiplexer_4_out_9, demultiplexer_4_out_10, demultiplexer_4_out_11,
       demultiplexer_5_out_1, demultiplexer_5_out_2, demultiplexer_5_out_3, demultiplexer_5_out_4,
       demultiplexer_5_out_5, demultiplexer_5_out_6, demultiplexer_5_out_7, demultiplexer_5_out_8,
       demultiplexer_5_out_9, demultiplexer_5_out_10, demultiplexer_5_out_11, demultiplexer_5_out_12,
       demultiplexer_5_out_13, demultiplexer_5_out_14, demultiplexer_5_out_15, demultiplexer_5_out_16,
       demultiplexer_5_out_17, demultiplexer_5_out_18, demultiplexer_5_out_19, demultiplexer_5_out_20,
       demultiplexer_5_out_21, demultiplexer_5_out_22, demultiplexer_5_out_23, demultiplexer_6_out_1,
       demultiplexer_6_out_2, demultiplexer_6_out_3, demultiplexer_6_out_4, demultiplexer_6_out_5,
       demultiplexer_6_out_6, demultiplexer_6_out_7, demultiplexer_6_out_8, demultiplexer_6_out_9,
       demultiplexer_6_out_10, demultiplexer_6_out_11, demultiplexer_6_out_12, demultiplexer_6_out_13,
       demultiplexer_6_out_14, demultiplexer_6_out_15, demultiplexer_6_out_16, demultiplexer_6_out_17,
       demultiplexer_6_out_18, demultiplexer_6_out_19, demultiplexer_6_out_20, demultiplexer_6_out_21,
       demultiplexer_6_out_22, demultiplexer_6_out_23, DMA_clr, DMA_out, driverinvsel_24_out, FLAG_C, FLAG_V,
       IRJ_clr, IRJ_out, IRJ_Vout, IRK_clr, IRK_out, IRK_Vout, IRQ_en, IX_clr, IY_clr, memory_map_state_1_q0,
       memory_map_state_1_q1, memory_map_state_1_q3, memory_map_state_1_q4, nA_DATout, nA_st, nADD_ADSout,
       nB_DATout, nB_st, nBC_ADSout, nBIT_DATout, nC_DATout, nC_Fst, nC_st, nD_DATout, nD_Fst, nD_st,
       nF2_DATout, nF_ALUin, nF_DATin, nF_DATout, nIR_st, nIX_ADSout, nIXH_DATout, nIXH_st, nIXL_DATout,
       nIXL_st, nIY_ADSout, nIYH_DATout, nIYH_st, nIYL_DATout, nIYL_st, nJ_Fst, nK_Fst, nMAR_ADSout,
       nMARH_st, nMARL_st, nMDRH_DATout, nMDRH_st, nMDRL_DATout, nMDRL_st, nMEM_DATout, nMEM_en, nMEM_in,
       NMI_Vout, nNZ_Fst, nor_1_out, nor_2_out, nor_3_out, not_14_out, not_15_out, not_16_out, not_17_out,
       not_18_out, not_19_out, not_20_out, not_21_out, not_22_out, not_24_out, not_25_out, not_26_out,
       not_31_out, not_63_out, not_64_out, not_65_out, not_67_out, not_68_out, not_69_out, not_70_out,
       not_71_out, not_72_out, not_81_out, nPC_ADSout, nPCH_DATout, nPCH_st, nPCL_DATout, nPCL_st,
       nREG_ADDin, nREG_DATin, nSEQ_en, nSEQ_st, nSP_ADSout, nSP_DATout, nSP_st, nSUM_DATout, nSUM_st,
       nTADD_st, nTMEM_st, nV_Fst, nX_Fst, nY_Fst, or_2_out, or_3_out, or_7_out, or_8_out, or_11_out,
       or_13_out, or_14_out, or_20_out, or_27_out, or_28_out, or_29_out, PC_en, PCL_ovf, pulldown_59_out,
       RST_Vout, SEQ_val, SP_dir, SP_en, t_ff_1_nq, t_ff_1_q, X_FTdat, Y_FTdat, \Σ_Csel , \Σ_Cval , \Σ_M ,
       \Σ_rot ;
  wire [1:0] alu_1_p11, d_ff_1_q, FLAG_NZ, MD_q;
  wire [2:0] A_sel, C_sel, or_1_out, or_9_out, or_10_out, Z_sel;
  wire [3:0] F_sel, or_12_out, \Σ_sel ;
  wire [4:0] B_sel, or_15_out, or_19_out, R_sel, \µSEQ_out ;
  wire [7:0] A_out, add_1_s, add_2_s, ADDRESS_HIin, ADDRESS_HIout, ADDRESS_LOin, ADDRESS_LOout, alu_1_p1,
       B_out, bitextender_1_out, bitextender_2_out, C_out, D_out, DATA_out, driverinvsel_20_out,
       driverinvsel_21_out, driverinvsel_22_out, driverinvsel_23_out, driverinvsel_36_out,
       driverinvsel_37_out, driverinvsel_38_out, driverinvsel_39_out, driverinvsel_50_out,
       driverinvsel_51_out, driverinvsel_52_out, driverinvsel_53_out, IR_q, IXL_out, IYL_out, MARH_q, MARL_q,
       MDRH_q, MDRL_q, or_16_out, or_17_out, or_18_out, or_21_out, or_22_out, or_23_out, or_24_out,
       or_25_out, or_26_out, PCH_out, PCL_out, ramsingleportsel_1_d, register_1_q, register_2_q,
       register_3_q, REL_q, rom_1_d, SP_out, TSR_q;
  wire [7:6] DATA_in;
  wire [11:5] DMA_2_q;
  wire [15:8] IXH_out, IYH_out;
  wire [47:0] \µCODE_d ;
  wire [47:33] CTRL_q;

  CounterPreset u_DMA (
    .en(~1'b1), .C(CLK2), .dir(1'b0), .in(D1), .ld(~nD_Fst), .clr(DMA_clr), .out(DMA_out));  // open: ovf
  CounterPreset u_IRJ (
    .en(~1'b1), .C(CLK2), .dir(1'b0), .in(D1), .ld(~nJ_Fst), .clr(IRJ_clr), .out(IRJ_out));  // open: ovf
  CounterPreset u_IRK (
    .en(~1'b1), .C(CLK2), .dir(1'b0), .in(D1), .ld(~nK_Fst), .clr(IRK_clr), .out(IRK_out));  // open: ovf
  assign or_1_out = Z_sel | Zsel;  // Or or_1, 3 bits wide
  and and_1 (and_1_out, ~COND_N, FLAG_NZ[0]);  // And
  Demultiplexer #(.Selector_Bits(3)) demultiplexer_1 (
    .sel(or_1_out), .in(1'b1), .out_1(demultiplexer_1_out_1), .out_2(demultiplexer_1_out_2),
    .out_3(demultiplexer_1_out_3), .out_4(BCD_clr), .out_5(DMA_clr), .out_6(IRK_clr), .out_7(IRJ_clr));  // open: out_0
  assign D2 = ~nF2_DATout ? IRJ_out : 1'bz;  // DriverInvSel driverinvsel_1
  assign D1 = ~nF2_DATout ? DMA_out : 1'bz;  // DriverInvSel driverinvsel_2
  PullDown pulldown_1 (.out(D1));
  PullDown pulldown_2 (.out(D2));
  and and_2 (and_2_out, ~COND_Z, FLAG_NZ[1]);  // And
  Register #(.Bits(2)) MD (.D({D2, D1}), .C(CLK2), .en(~memory_map_state_1_q3), .Q(MD_q));
  Register #(.Bits(8)) IO (.D({DATA_in, D6, D5, D4, D3, D2, D1}), .C(CLK2), .en(~memory_map_state_1_q4));  // open: Q
  assign D3 = ~nF2_DATout ? IRK_out : 1'bz;  // DriverInvSel driverinvsel_3
  PullDown pulldown_3 (.out(D3));
  and and_3 (and_3_out, ~CONV_V, FLAG_V);  // And
  and and_4 (and_4_out, ~COND_C, ~FLAG_C);  // And
  D_FF #(.Bits(2)) d_ff_1 (.D(MD_q), .C(CLK1), .Q(d_ff_1_q));  // open: nQ
  or or_2 (or_2_out, and_1_out, and_2_out);
  and and_5 (and_5_out, ~COND_X, X_FTdat);  // And
  nor nor_1 (nor_1_out, ~DMA, DMA_out);  // NOr
  nor nor_2 (nor_2_out, ~IRJ, IRJ_out);  // NOr
  nor nor_3 (nor_3_out, ~IRK, IRK_out);  // NOr
  or or_3 (or_3_out, and_3_out, and_4_out);
  and and_6 (and_6_out, ~COND_Y, Y_FTdat);  // And
  or or_4 (A_clr, demultiplexer_1_out_1, BCD_clr);
  or or_5 (IX_clr, demultiplexer_1_out_2, BCD_clr);
  or or_6 (IY_clr, demultiplexer_1_out_3, BCD_clr);
  MEMORY_MAP_STATE memory_map_state_1 (
    .A({ADDRESS_HIin, ADDRESS_LOin}), .WR(nMEM_in), .MD(d_ff_1_q), .EN(nMEM_en), .Q4(memory_map_state_1_q4),
    .Q3(memory_map_state_1_q3), .Q1(memory_map_state_1_q1), .Q0(memory_map_state_1_q0));  // open: Q2
  and and_7 (and_7_out, nor_1_out, IRQ_en);
  and and_8 (and_8_out, RST, IRQ_en);
  and and_9 (and_9_out, NMI, IRQ_en);
  and and_10 (and_10_out, nor_2_out, IRQ_en);
  and and_11 (and_11_out, nor_3_out, IRQ_en);
  and and_12 (and_12_out, HALT, IRQ_en);
  or or_7 (or_7_out, and_5_out, and_6_out);
  or or_8 (or_8_out, or_3_out, or_7_out);
  CounterPreset #(.Bits(5)) \u_µSEQ  (
    .en(~nSEQ_en), .C(CLK2), .dir(1'b0), .in({4'b0000, SEQ_val}), .ld(~nSEQ_st), .clr(1'b0), .out(\µSEQ_out ));  // open: ovf
  D_FF DMA_2 (.D(and_7_out), .C(CLK2), .Q(DMA_2_q[5]));  // open: nQ
  D_FF RESET (.D(and_8_out), .C(CLK2), .Q(DMA_2_q[6]));  // open: nQ
  D_FF u_NMI (.D(and_9_out), .C(CLK2), .Q(DMA_2_q[7]));  // open: nQ
  D_FF IRJ_2 (.D(and_10_out), .C(CLK2), .Q(DMA_2_q[8]));  // open: nQ
  D_FF IRK_2 (.D(and_11_out), .C(CLK2), .Q(DMA_2_q[9]));  // open: nQ
  D_FF u_HALT (.D(and_12_out), .C(CLK2), .Q(DMA_2_q[10]));  // open: nQ
  D_FF COND (.D(COND_RES), .C(CLK2), .Q(DMA_2_q[11]));  // open: nQ
  Register #(.Bits(8)) IR (.D({DATA_in, D6, D5, D4, D3, D2, D1}), .C(CLK2), .en(~nIR_st), .Q(IR_q));
  Demultiplexer #(.Selector_Bits(3)) demultiplexer_2 (
    .sel(or_9_out), .in(1'b1), .out_1(demultiplexer_2_out_1), .out_2(demultiplexer_2_out_2),
    .out_3(demultiplexer_2_out_3), .out_4(demultiplexer_2_out_4), .out_5(demultiplexer_2_out_5),
    .out_6(demultiplexer_2_out_6), .out_7(demultiplexer_2_out_7));  // open: out_0
  assign or_9_out = A_sel | Asel;  // Or or_9, 3 bits wide
  Demultiplexer #(.Selector_Bits(3)) demultiplexer_3 (
    .sel(or_10_out), .in(1'b1), .out_1(demultiplexer_3_out_1), .out_2(demultiplexer_3_out_2),
    .out_3(demultiplexer_3_out_3), .out_4(demultiplexer_3_out_4), .out_5(demultiplexer_3_out_5),
    .out_6(demultiplexer_3_out_6));  // open: out_0, out_7
  assign or_10_out = C_sel | Csel;  // Or or_10, 3 bits wide
  or or_11 (or_11_out, or_2_out, or_8_out);
  not not_1 (nBC_ADSout, demultiplexer_2_out_1);
  not not_2 (nPC_ADSout, demultiplexer_2_out_2);
  not not_3 (nSP_ADSout, demultiplexer_2_out_3);
  not not_4 (nIX_ADSout, demultiplexer_2_out_4);
  not not_5 (nIY_ADSout, demultiplexer_2_out_5);
  not not_6 (nMAR_ADSout, demultiplexer_2_out_6);
  not not_7 (nADD_ADSout, demultiplexer_2_out_7);
  not not_8 (COND_N, demultiplexer_3_out_1);
  not not_9 (COND_Z, demultiplexer_3_out_2);
  not not_10 (CONV_V, demultiplexer_3_out_3);
  not not_11 (COND_C, demultiplexer_3_out_4);
  not not_12 (COND_X, demultiplexer_3_out_5);
  not not_13 (COND_Y, demultiplexer_3_out_6);
  RAMSinglePortSel #(.AddrBits(16), .Bits(8)) ramsingleportsel_1 (
    .A({ADDRESS_HIin, ADDRESS_LOin}), .CS(~memory_map_state_1_q0), .WE(~nMEM_in), .OE(~nMEM_DATout),
    .D(ramsingleportsel_1_d));
  ROM #(.AddrBits(16), .Bits(8)) rom_1 (.A({ADDRESS_HIin, ADDRESS_LOin}), .sel(not_14_out), .D(rom_1_d));
  not not_14 (not_14_out, memory_map_state_1_q1);
  not not_15 (not_15_out, or_11_out);
  assign COND_RES = ~COND_P ? or_11_out : 1'bz;  // DriverInvSel driverinvsel_4
  assign COND_RES = ~COND_N ? not_15_out : 1'bz;  // DriverInvSel driverinvsel_5
  Demultiplexer #(.Selector_Bits(4)) demultiplexer_4 (
    .sel(or_12_out), .in(1'b1), .out_1(demultiplexer_4_out_1), .out_2(demultiplexer_4_out_2),
    .out_3(demultiplexer_4_out_3), .out_4(demultiplexer_4_out_4), .out_5(demultiplexer_4_out_5),
    .out_6(demultiplexer_4_out_6), .out_7(demultiplexer_4_out_7), .out_8(demultiplexer_4_out_8),
    .out_9(demultiplexer_4_out_9), .out_10(demultiplexer_4_out_10), .out_11(demultiplexer_4_out_11));  // open: out_0, out_12, out_13, out_14, out_15
  assign or_12_out = F_sel | Fsel;  // Or or_12, 4 bits wide
  or or_13 (or_13_out, nMEM_DATout, memory_map_state_1_q0);
  or or_14 (or_14_out, nMEM_DATout, memory_map_state_1_q1);
  ROM #(.AddrBits(20), .Bits(48)) \u_µCODE  (.A({IR_q, DMA_2_q, \µSEQ_out }), .sel(1'b1), .D(\µCODE_d ));
  not not_16 (not_16_out, demultiplexer_4_out_1);
  not not_17 (not_17_out, demultiplexer_4_out_2);
  not not_18 (not_18_out, demultiplexer_4_out_3);
  not not_19 (not_19_out, demultiplexer_4_out_4);
  not not_20 (not_20_out, demultiplexer_4_out_5);
  not not_21 (not_21_out, demultiplexer_4_out_6);
  not not_22 (not_22_out, demultiplexer_4_out_7);
  not not_23 (nD_Fst, demultiplexer_4_out_8);
  not not_24 (not_24_out, demultiplexer_4_out_9);
  not not_25 (not_25_out, demultiplexer_4_out_10);
  not not_26 (not_26_out, demultiplexer_4_out_11);
  PullDown #(.Bits(8)) pulldown_4 (.out(ramsingleportsel_1_d));
  PullDown #(.Bits(8)) pulldown_5 (.out(rom_1_d));
  assign ramsingleportsel_1_d = ~nMEM_in ? register_1_q : 8'bz;  // DriverInvSel driverinvsel_6
  assign DATA_out = ~or_13_out ? ramsingleportsel_1_d : 8'bz;  // DriverInvSel driverinvsel_7
  assign DATA_out = ~or_14_out ? rom_1_d : 8'bz;  // DriverInvSel driverinvsel_8
  D_FF #(.Bits(48)) CTRL (
    .D(\µCODE_d ), .C(CLK1),
    .Q({CTRL_q[47:41], IRQ_en, SEQ_val, CTRL_q[38:37], nF_ALUin, nREG_DATin, CTRL_q[34:33], SP_dir, COND_P, \Σ_rot , \Σ_Cval , \Σ_Csel , \Σ_M , \Σ_sel , Z_sel, F_sel, C_sel, A_sel, B_sel, R_sel}));  // open: nQ
  Register #(.Bits(8)) register_1 (.D({DATA_in, D6, D5, D4, D3, D2, D1}), .C(CLK2), .en(~nTMEM_st), .Q(register_1_q));
  PullDown #(.Bits(8)) pulldown_6 (.out(DATA_out));
  not not_27 (SP_en, CTRL_q[33]);
  not not_28 (PC_en, CTRL_q[34]);
  not not_29 (nSEQ_en, CTRL_q[37]);
  not not_30 (nSEQ_st, CTRL_q[38]);
  not not_31 (not_31_out, Clock);
  PullDown pulldown_7 (.out(Clock));
  T_FF #(.withEnable("false")) t_ff_1 (.C(not_31_out), .Q(t_ff_1_q), .nQ(t_ff_1_nq));
  and and_13 (CLK1, Clock, t_ff_1_q);
  and and_14 (CLK2, t_ff_1_nq, ~nWAIT, Clock);  // And
  and and_15 (nNZ_Fst, not_16_out, not_22_out, not_19_out);
  and and_16 (nV_Fst, not_19_out, not_22_out, not_17_out);
  and and_17 (nC_Fst, not_19_out, not_22_out, not_18_out);
  and and_18 (nX_Fst, not_20_out, not_22_out);
  and and_19 (nY_Fst, not_21_out, not_22_out);
  and and_20 (nJ_Fst, not_24_out, not_26_out);
  and and_21 (nK_Fst, not_25_out, not_26_out);
  not not_32 (COND_N, COND_P);
  not not_33 (nREG_ADDin, nREG_DATin);
  not not_34 (nF_DATin, nF_ALUin);
  assign or_15_out = B_sel | Bsel;  // Or or_15, 5 bits wide
  Demultiplexer #(.Selector_Bits(5)) demultiplexer_5 (
    .sel(or_15_out), .in(1'b1), .out_1(demultiplexer_5_out_1), .out_2(demultiplexer_5_out_2),
    .out_3(demultiplexer_5_out_3), .out_4(demultiplexer_5_out_4), .out_5(demultiplexer_5_out_5),
    .out_6(demultiplexer_5_out_6), .out_7(demultiplexer_5_out_7), .out_8(demultiplexer_5_out_8),
    .out_9(demultiplexer_5_out_9), .out_10(demultiplexer_5_out_10), .out_11(demultiplexer_5_out_11),
    .out_12(demultiplexer_5_out_12), .out_13(demultiplexer_5_out_13), .out_14(demultiplexer_5_out_14),
    .out_15(demultiplexer_5_out_15), .out_16(demultiplexer_5_out_16), .out_17(demultiplexer_5_out_17),
    .out_18(demultiplexer_5_out_18), .out_19(demultiplexer_5_out_19), .out_20(demultiplexer_5_out_20),
    .out_21(demultiplexer_5_out_21), .out_22(demultiplexer_5_out_22), .out_23(demultiplexer_5_out_23));  // open: out_0, out_24, out_25, out_26, out_27, out_28, out_29, out_30, out_31
  not not_35 (nA_DATout, demultiplexer_5_out_1);
  not not_36 (nB_DATout, demultiplexer_5_out_2);
  not not_37 (nC_DATout, demultiplexer_5_out_3);
  not not_38 (nD_DATout, demultiplexer_5_out_4);
  not not_39 (nF_DATout, demultiplexer_5_out_5);
  not not_40 (nF2_DATout, demultiplexer_5_out_6);
  not not_41 (nPCH_DATout, demultiplexer_5_out_7);
  not not_42 (nPCL_DATout, demultiplexer_5_out_8);
  not not_43 (nSP_DATout, demultiplexer_5_out_9);
  not not_44 (nIXH_DATout, demultiplexer_5_out_10);
  not not_45 (nIXL_DATout, demultiplexer_5_out_11);
  not not_46 (nIYH_DATout, demultiplexer_5_out_12);
  not not_47 (nIYL_DATout, demultiplexer_5_out_13);
  not not_48 (nMDRH_DATout, demultiplexer_5_out_14);
  not not_49 (nMDRL_DATout, demultiplexer_5_out_15);
  not not_50 (nSUM_DATout, demultiplexer_5_out_16);
  not not_51 (nMEM_DATout, demultiplexer_5_out_17);
  not not_52 (nBIT_DATout, demultiplexer_5_out_18);
  not not_53 (RST_Vout, demultiplexer_5_out_19);
  not not_54 (NMI_Vout, demultiplexer_5_out_20);
  not not_55 (BRK_Vout, demultiplexer_5_out_21);
  not not_56 (IRJ_Vout, demultiplexer_5_out_22);
  not not_57 (IRK_Vout, demultiplexer_5_out_23);
  PullDown #(.Bits(8)) pulldown_8 (.out(ADDRESS_LOout));
  PullDown #(.Bits(8)) pulldown_9 (.out(ADDlo));
  PullDown #(.Bits(8)) pulldown_10 (.out(ADDRESS_HIout));
  PullDown #(.Bits(8)) pulldown_11 (.out(ADDhi));
  PullDown #(.Bits(8)) pulldown_12 (.out(DATA_out));
  PullDown #(.Bits(8)) pulldown_13 (.out(DAT));
  assign or_16_out = ADDRESS_LOout | ADDlo;  // Or or_16, 8 bits wide
  assign or_17_out = ADDRESS_HIout | ADDhi;  // Or or_17, 8 bits wide
  assign or_18_out = DATA_out | DAT;  // Or or_18, 8 bits wide
  assign or_19_out = R_sel | Rsel;  // Or or_19, 5 bits wide
  Demultiplexer #(.Selector_Bits(5)) demultiplexer_6 (
    .sel(or_19_out), .in(1'b1), .out_1(demultiplexer_6_out_1), .out_2(demultiplexer_6_out_2),
    .out_3(demultiplexer_6_out_3), .out_4(demultiplexer_6_out_4), .out_5(demultiplexer_6_out_5),
    .out_6(demultiplexer_6_out_6), .out_7(demultiplexer_6_out_7), .out_8(demultiplexer_6_out_8),
    .out_9(demultiplexer_6_out_9), .out_10(demultiplexer_6_out_10), .out_11(demultiplexer_6_out_11),
    .out_12(demultiplexer_6_out_12), .out_13(demultiplexer_6_out_13), .out_14(demultiplexer_6_out_14),
    .out_15(demultiplexer_6_out_15), .out_16(demultiplexer_6_out_16), .out_17(demultiplexer_6_out_17),
    .out_18(demultiplexer_6_out_18), .out_19(demultiplexer_6_out_19), .out_20(demultiplexer_6_out_20),
    .out_21(demultiplexer_6_out_21), .out_22(demultiplexer_6_out_22), .out_23(demultiplexer_6_out_23));  // open: out_0, out_24, out_25, out_26, out_27, out_28, out_29, out_30, out_31
  DiodeForward diodeforward_1 (.in(or_16_out[0]), .out(ADDRESS_LOin[0]));
  DiodeForward diodeforward_2 (.in(or_16_out[1]), .out(ADDRESS_LOin[1]));
  DiodeForward diodeforward_3 (.in(or_16_out[2]), .out(ADDRESS_LOin[2]));
  DiodeForward diodeforward_4 (.in(or_16_out[3]), .out(ADDRESS_LOin[3]));
  DiodeForward diodeforward_5 (.in(or_16_out[4]), .out(ADDRESS_LOin[4]));
  DiodeForward diodeforward_6 (.in(or_16_out[5]), .out(ADDRESS_LOin[5]));
  DiodeForward diodeforward_7 (.in(or_16_out[6]), .out(ADDRESS_LOin[6]));
  DiodeForward diodeforward_8 (.in(or_16_out[7]), .out(ADDRESS_LOin[7]));
  DiodeForward diodeforward_9 (.in(or_17_out[0]), .out(ADDRESS_HIin[0]));
  DiodeForward diodeforward_10 (.in(or_17_out[1]), .out(ADDRESS_HIin[1]));
  DiodeForward diodeforward_11 (.in(or_17_out[2]), .out(ADDRESS_HIin[2]));
  DiodeForward diodeforward_12 (.in(or_17_out[3]), .out(ADDRESS_HIin[3]));
  DiodeForward diodeforward_13 (.in(or_17_out[4]), .out(ADDRESS_HIin[4]));
  DiodeForward diodeforward_14 (.in(or_17_out[5]), .out(ADDRESS_HIin[5]));
  DiodeForward diodeforward_15 (.in(or_17_out[6]), .out(ADDRESS_HIin[6]));
  DiodeForward diodeforward_16 (.in(or_17_out[7]), .out(ADDRESS_HIin[7]));
  PullDown pulldown_14 (.out(ADDRESS_HIin[7]));
  PullDown pulldown_15 (.out(ADDRESS_HIin[6]));
  assign ADDRESS_LOout = ~RST_Vout ? 8'hf9 : 8'bz;  // DriverInvSel driverinvsel_9
  assign ADDRESS_HIout = ~RST_Vout ? {8{1'b1}} : 8'bz;  // DriverInvSel driverinvsel_10
  assign ADDRESS_LOout = ~NMI_Vout ? {8{1'b1}} : 8'bz;  // DriverInvSel driverinvsel_11
  assign ADDRESS_HIout = ~NMI_Vout ? 8'hf7 : 8'bz;  // DriverInvSel driverinvsel_12
  assign ADDRESS_LOout = ~BRK_Vout ? {8{1'b1}} : 8'bz;  // DriverInvSel driverinvsel_13
  assign ADDRESS_HIout = ~BRK_Vout ? 8'hf5 : 8'bz;  // DriverInvSel driverinvsel_14
  assign ADDRESS_LOout = ~IRJ_Vout ? {8{1'b1}} : 8'bz;  // DriverInvSel driverinvsel_15
  assign ADDRESS_HIout = ~IRJ_Vout ? 8'hf3 : 8'bz;  // DriverInvSel driverinvsel_16
  assign ADDRESS_LOout = ~IRK_Vout ? {8{1'b1}} : 8'bz;  // DriverInvSel driverinvsel_17
  assign ADDRESS_HIout = ~IRK_Vout ? 8'hf1 : 8'bz;  // DriverInvSel driverinvsel_18
  not not_58 (nA_st, demultiplexer_6_out_1);
  not not_59 (nB_st, demultiplexer_6_out_2);
  not not_60 (nC_st, demultiplexer_6_out_3);
  not not_61 (nD_st, demultiplexer_6_out_4);
  not not_62 (nIR_st, demultiplexer_6_out_5);
  not not_63 (not_63_out, demultiplexer_6_out_6);
  not not_64 (not_64_out, demultiplexer_6_out_7);
  not not_65 (not_65_out, demultiplexer_6_out_8);
  not not_66 (nSP_st, demultiplexer_6_out_9);
  not not_67 (not_67_out, demultiplexer_6_out_10);
  not not_68 (not_68_out, demultiplexer_6_out_11);
  not not_69 (not_69_out, demultiplexer_6_out_12);
  not not_70 (not_70_out, demultiplexer_6_out_13);
  not not_71 (not_71_out, demultiplexer_6_out_14);
  not not_72 (not_72_out, demultiplexer_6_out_15);
  not not_73 (nMDRH_st, demultiplexer_6_out_16);
  not not_74 (nMDRL_st, demultiplexer_6_out_17);
  not not_75 (nMARH_st, demultiplexer_6_out_18);
  not not_76 (nMARL_st, demultiplexer_6_out_19);
  not not_77 (nSUM_st, demultiplexer_6_out_20);
  not not_78 (nMEM_in, demultiplexer_6_out_21);
  not not_79 (nTMEM_st, demultiplexer_6_out_22);
  not not_80 (nTADD_st, demultiplexer_6_out_23);
  PullDown pulldown_16 (.out(ADDRESS_HIin[5]));
  PullDown pulldown_17 (.out(ADDRESS_HIin[4]));
  PullDown pulldown_18 (.out(ADDRESS_HIin[3]));
  PullDown pulldown_19 (.out(ADDRESS_HIin[2]));
  PullDown #(.Bits(8)) pulldown_20 (.out(ADDRESS_LOout));
  PullDown #(.Bits(8)) pulldown_21 (.out(ADDRESS_HIout));
  PullDown pulldown_22 (.out(ADDRESS_LOin[7]));
  PullDown pulldown_23 (.out(ADDRESS_LOin[6]));
  PullDown pulldown_24 (.out(ADDRESS_HIin[1]));
  PullDown pulldown_25 (.out(ADDRESS_HIin[0]));
  DiodeForward diodeforward_17 (.in(or_18_out[0]), .out(D1));
  DiodeForward diodeforward_18 (.in(or_18_out[1]), .out(D2));
  DiodeForward diodeforward_19 (.in(or_18_out[2]), .out(D3));
  DiodeForward diodeforward_20 (.in(or_18_out[3]), .out(D4));
  DiodeForward diodeforward_21 (.in(or_18_out[4]), .out(D5));
  DiodeForward diodeforward_22 (.in(or_18_out[5]), .out(D6));
  DiodeForward diodeforward_23 (.in(or_18_out[6]), .out(DATA_in[6]));
  DiodeForward diodeforward_24 (.in(or_18_out[7]), .out(DATA_in[7]));
  PullDown pulldown_26 (.out(DATA_in[7]));
  PullDown pulldown_27 (.out(DATA_in[6]));
  assign DATA_out = ~nBIT_DATout ? {8{1'b1}} : 8'bz;  // DriverInvSel driverinvsel_19
  PullDown pulldown_28 (.out(ADDRESS_LOin[5]));
  PullDown pulldown_29 (.out(ADDRESS_LOin[4]));
  PullDown pulldown_30 (.out(ADDRESS_LOin[3]));
  PullDown pulldown_31 (.out(ADDRESS_LOin[2]));
  PullDown pulldown_32 (.out(D6));
  PullDown pulldown_33 (.out(D5));
  PullDown pulldown_34 (.out(D4));
  PullDown pulldown_35 (.out(D3));
  and and_22 (nPCH_st, not_63_out, not_64_out);
  and and_23 (nPCL_st, not_63_out, not_65_out);
  and and_24 (nIXH_st, not_67_out, not_68_out);
  and and_25 (nIXL_st, not_67_out, not_69_out);
  and and_26 (nIYH_st, not_70_out, not_71_out);
  and and_27 (nIYL_st, not_70_out, not_72_out);
  and and_28 (nMEM_en, nMEM_in, nMEM_DATout);
  PullDown pulldown_36 (.out(ADDRESS_LOin[1]));
  PullDown pulldown_37 (.out(ADDRESS_LOin[0]));
  PullDown pulldown_38 (.out(D2));
  PullDown pulldown_39 (.out(D1));
  PullDown #(.Bits(8)) pulldown_40 (.out(DATA_out));
  or or_20 (or_20_out, CLK2, A_clr);
  assign driverinvsel_20_out = ~nREG_DATin ? {DATA_in, D6, D5, D4, D3, D2, D1} : 8'bz;  // DriverInvSel driverinvsel_20
  assign driverinvsel_21_out = ~nREG_ADDin ? ADDRESS_LOin : 8'bz;  // DriverInvSel driverinvsel_21
  PullDown #(.Bits(8)) pulldown_41 (.out(driverinvsel_21_out));
  assign driverinvsel_22_out = ~nREG_DATin ? {DATA_in, D6, D5, D4, D3, D2, D1} : 8'bz;  // DriverInvSel driverinvsel_22
  assign driverinvsel_23_out = ~nREG_ADDin ? ADDRESS_HIin : 8'bz;  // DriverInvSel driverinvsel_23
  CounterPreset #(.Bits(8)) A (
    .en(~1'b1), .C(or_20_out), .dir(1'b0), .in({DATA_in, D6, D5, D4, D3, D2, D1}), .ld(~nA_st), .clr(A_clr),
    .out(A_out));  // open: ovf
  assign or_21_out = driverinvsel_20_out | driverinvsel_21_out;  // Or or_21, 8 bits wide
  Register X_F (.D(driverinvsel_24_out), .C(CLK2), .en(~nY_Fst), .Q(Y_FTdat));
  assign driverinvsel_24_out = ~nF_DATin ? D5 : 1'bz;  // DriverInvSel driverinvsel_24
  PullDown pulldown_42 (.out(driverinvsel_24_out));
  assign or_22_out = driverinvsel_22_out | driverinvsel_23_out;  // Or or_22, 8 bits wide
  PullDown #(.Bits(8)) pulldown_43 (.out(driverinvsel_23_out));
  Register #(.Bits(8)) MDRL (.D({DATA_in, D6, D5, D4, D3, D2, D1}), .C(CLK2), .en(~nMDRL_st), .Q(MDRL_q));
  Register #(.Bits(8)) MDRH (.D({DATA_in, D6, D5, D4, D3, D2, D1}), .C(CLK2), .en(~nMDRH_st), .Q(MDRH_q));
  PullDown #(.Bits(8)) pulldown_44 (.out(or_21_out));
  assign driverinvsel_24_out = ~nF_ALUin ? comparator_1_eq : 1'bz;  // DriverInvSel driverinvsel_25
  PullDown #(.Bits(8)) pulldown_45 (.out(or_22_out));
  assign DATA_out = ~nA_DATout ? A_out : 8'bz;  // DriverInvSel driverinvsel_26
  PullDown #(.Bits(8)) pulldown_46 (.out(DATA_out));
  CounterPreset #(.Bits(8)) IYL (
    .en(~1'b1), .C(CLK2), .dir(1'b0), .in(or_21_out), .ld(~nIYL_st), .clr(IY_clr), .out(IYL_out));  // open: ovf
  CounterPreset #(.Bits(8)) IYH (
    .en(~1'b1), .C(CLK2), .dir(1'b0), .in(or_22_out), .ld(~nIYH_st), .clr(IY_clr), .out(IYH_out));  // open: ovf
  Comparator #(.Bits(16)) comparator_1 (.a({IYH_out, IYL_out}), .b({16{1'b0}}), .eq(comparator_1_eq));  // open: gt, lt
  assign DATA_out = ~nSUM_DATout ? TSR_q : 8'bz;  // DriverInvSel driverinvsel_27
  PullDown #(.Bits(8)) pulldown_47 (.out(DATA_out));
  assign ADDRESS_LOout = ~nIY_ADSout ? IYL_out : 8'bz;  // DriverInvSel driverinvsel_28
  assign DATA_out = ~nIYL_DATout ? IYL_out : 8'bz;  // DriverInvSel driverinvsel_29
  assign ADDRESS_HIout = ~nIY_ADSout ? IYH_out : 8'bz;  // DriverInvSel driverinvsel_30
  assign DATA_out = ~nIXH_DATout ? IYH_out : 8'bz;  // DriverInvSel driverinvsel_31
  assign DATA_out = ~nMDRL_DATout ? MDRL_q : 8'bz;  // DriverInvSel driverinvsel_32
  PullDown #(.Bits(8)) pulldown_48 (.out(DATA_out));
  assign DATA_out = ~nMDRH_DATout ? MDRH_q : 8'bz;  // DriverInvSel driverinvsel_33
  PullDown #(.Bits(8)) pulldown_49 (.out(DATA_out));
  PullDown #(.Bits(8)) pulldown_50 (.out(DATA_out));
  PullDown #(.Bits(8)) pulldown_51 (.out(ADDRESS_LOout));
  PullDown #(.Bits(8)) pulldown_52 (.out(DATA_out));
  PullDown #(.Bits(8)) pulldown_53 (.out(ADDRESS_HIout));
  Register #(.Bits(8)) TSR (.D(alu_1_p1), .C(CLK2), .en(~nSUM_st), .Q(TSR_q));
  PullDown #(.Bits(8)) pulldown_54 (.out(DATA_out));
  // ALU alu_1: pin names not known; wires that end beside it: alu_1_p1, \Σ_rot , \Σ_Csel , \Σ_Cval , A_out, FLAG_C, {DATA_in, D6, D5, D4, D3, D2, D1}, nF_ALUin, \Σ_M , \Σ_sel , alu_1_p11[1], alu_1_p11[0], alu_1_p13, alu_1_p14
  Register #(.Bits(8)) MARL (.D({DATA_in, D6, D5, D4, D3, D2, D1}), .C(CLK2), .en(~nMARL_st), .Q(MARL_q));
  Register #(.Bits(8)) MARH (.D({DATA_in, D6, D5, D4, D3, D2, D1}), .C(CLK2), .en(~nMARH_st), .Q(MARH_q));
  assign DATA_out = ~nF_DATout ? {2'b00, Y_FTdat, X_FTdat, FLAG_C, FLAG_V, FLAG_NZ} : 8'bz;  // DriverInvSel driverinvsel_34
  PullDown #(.Bits(2)) pulldown_55 (.out(alu_1_p11));
  Register #(.Bits(2)) NZ_F (.D(alu_1_p11), .C(CLK2), .en(~nNZ_Fst), .Q(FLAG_NZ));
  PullDown pulldown_56 (.out(alu_1_p14));
  PullDown pulldown_57 (.out(alu_1_p13));
  assign alu_1_p11 = ~nF_DATin ? {D2, D1} : 2'bz;  // DriverInvSel driverinvsel_35
  assign driverinvsel_36_out = ~nREG_ADDin ? ADDRESS_LOin : 8'bz;  // DriverInvSel driverinvsel_36
  assign driverinvsel_37_out = ~nREG_ADDin ? ADDRESS_HIin : 8'bz;  // DriverInvSel driverinvsel_37
  assign driverinvsel_38_out = ~nREG_DATin ? {DATA_in, D6, D5, D4, D3, D2, D1} : 8'bz;  // DriverInvSel driverinvsel_38
  assign or_23_out = driverinvsel_38_out | driverinvsel_36_out;  // Or or_23, 8 bits wide
  PullDown #(.Bits(8)) pulldown_58 (.out(driverinvsel_36_out));
  Register X_F_2 (.D(pulldown_59_out), .C(CLK2), .en(~nX_Fst), .Q(X_FTdat));
  PullDown pulldown_59 (.out(pulldown_59_out));
  assign driverinvsel_39_out = ~nREG_DATin ? {DATA_in, D6, D5, D4, D3, D2, D1} : 8'bz;  // DriverInvSel driverinvsel_39
  assign or_24_out = driverinvsel_39_out | driverinvsel_37_out;  // Or or_24, 8 bits wide
  PullDown #(.Bits(8)) pulldown_60 (.out(driverinvsel_37_out));
  Register V_F (.D(alu_1_p14), .C(CLK2), .en(~nV_Fst), .Q(FLAG_V));
  assign alu_1_p14 = ~nF_DATin ? D3 : 1'bz;  // DriverInvSel driverinvsel_40
  PullDown #(.Bits(8)) pulldown_61 (.out(or_23_out));
  assign pulldown_59_out = ~nF_DATin ? D5 : 1'bz;  // DriverInvSel driverinvsel_41
  PullDown #(.Bits(8)) pulldown_62 (.out(or_24_out));
  assign ADDRESS_LOout = ~nMAR_ADSout ? MARL_q : 8'bz;  // DriverInvSel driverinvsel_42
  PullDown #(.Bits(8)) pulldown_63 (.out(ADDRESS_LOout));
  assign ADDRESS_HIout = ~nMAR_ADSout ? MARH_q : 8'bz;  // DriverInvSel driverinvsel_43
  PullDown #(.Bits(8)) pulldown_64 (.out(ADDRESS_HIout));
  Register nC_F (.D(alu_1_p13), .C(CLK2), .en(~nC_Fst), .Q(FLAG_C));
  assign alu_1_p13 = ~nF_DATin ? D4 : 1'bz;  // DriverInvSel driverinvsel_44
  CounterPreset #(.Bits(8)) IXL (
    .en(~1'b1), .C(CLK2), .dir(1'b0), .in(or_23_out), .ld(~nIXL_st), .clr(IX_clr), .out(IXL_out));  // open: ovf
  assign pulldown_59_out = ~nF_ALUin ? comparator_2_eq : 1'bz;  // DriverInvSel driverinvsel_45
  CounterPreset #(.Bits(8)) IXH (
    .en(~1'b1), .C(CLK2), .dir(1'b0), .in(or_24_out), .ld(~nIXH_st), .clr(IX_clr), .out(IXH_out));  // open: ovf
  Comparator #(.Bits(16)) comparator_2 (.a({IXH_out, IXL_out}), .b({16{1'b0}}), .eq(comparator_2_eq));  // open: gt, lt
  assign DATA_out = ~nIXL_DATout ? IXL_out : 8'bz;  // DriverInvSel driverinvsel_46
  assign DATA_out = ~nIXH_DATout ? IXH_out : 8'bz;  // DriverInvSel driverinvsel_47
  assign ADDRESS_LOout = ~nIX_ADSout ? IXL_out : 8'bz;  // DriverInvSel driverinvsel_48
  PullDown #(.Bits(8)) pulldown_65 (.out(DATA_out));
  PullDown #(.Bits(8)) pulldown_66 (.out(ADDRESS_LOout));
  assign ADDRESS_HIout = ~nIX_ADSout ? IXH_out : 8'bz;  // DriverInvSel driverinvsel_49
  PullDown #(.Bits(8)) pulldown_67 (.out(DATA_out));
  PullDown #(.Bits(8)) pulldown_68 (.out(ADDRESS_HIout));
  assign driverinvsel_50_out = ~nREG_DATin ? {DATA_in, D6, D5, D4, D3, D2, D1} : 8'bz;  // DriverInvSel driverinvsel_50
  assign driverinvsel_51_out = ~nREG_ADDin ? ADDRESS_LOin : 8'bz;  // DriverInvSel driverinvsel_51
  assign driverinvsel_52_out = ~nREG_DATin ? {DATA_in, D6, D5, D4, D3, D2, D1} : 8'bz;  // DriverInvSel driverinvsel_52
  assign driverinvsel_53_out = ~nREG_ADDin ? ADDRESS_HIin : 8'bz;  // DriverInvSel driverinvsel_53
  assign or_25_out = driverinvsel_50_out | driverinvsel_51_out;  // Or or_25, 8 bits wide
  PullDown #(.Bits(8)) pulldown_69 (.out(driverinvsel_51_out));
  PullDown #(.Bits(8)) pulldown_70 (.out(driverinvsel_50_out));
  assign or_26_out = driverinvsel_52_out | driverinvsel_53_out;  // Or or_26, 8 bits wide
  PullDown #(.Bits(8)) pulldown_71 (.out(driverinvsel_53_out));
  PullDown #(.Bits(8)) pulldown_72 (.out(driverinvsel_52_out));
  CounterPreset #(.Bits(8)) SP (
    .en(~SP_en), .C(CLK2), .dir(SP_dir), .in({DATA_in, D6, D5, D4, D3, D2, D1}), .ld(~nSP_st), .clr(1'b0),
    .out(SP_out));  // open: ovf
  PullDown #(.Bits(8)) pulldown_73 (.out(or_25_out));
  PullDown #(.Bits(8)) pulldown_74 (.out(or_26_out));
  LED u_D6 (.in(DATA_in[6]));
  LED D7 (.in(DATA_in[7]));
  LED A14 (.in(ADDRESS_HIin[6]));
  LED A15 (.in(ADDRESS_HIin[7]));
  not not_81 (not_81_out, PCL_ovf);
  LED u_D5 (.in(D6));
  LED A13 (.in(ADDRESS_HIin[5]));
  Register #(.Bits(8)) REL (.D({DATA_in, D6, D5, D4, D3, D2, D1}), .C(CLK2), .en(~nTADD_st), .Q(REL_q));
  CounterPreset #(.Bits(8)) PCL (
    .en(~PC_en), .C(CLK2), .dir(pcd), .in(or_25_out), .ld(~nPCL_st), .clr(1'b0), .out(PCL_out), .ovf(PCL_ovf));
  CounterPreset #(.Bits(8)) PCH (
    .en(~not_81_out), .C(CLK2), .dir(pcd), .in(or_26_out), .ld(~nPCH_st), .clr(1'b0), .out(PCH_out));  // open: ovf
  or or_27 (or_27_out, CLK2, BCD_clr);
  or or_28 (or_28_out, CLK2, BCD_clr);
  or or_29 (or_29_out, CLK2, BCD_clr);
  assign DATA_out = ~nSP_DATout ? SP_out : 8'bz;  // DriverInvSel driverinvsel_54
  LED u_D4 (.in(D5));
  LED A12 (.in(ADDRESS_HIin[4]));
  assign ADDRESS_HIout = ~nSP_ADSout ? 8'h1 : 8'bz;  // DriverInvSel driverinvsel_55
  assign ADDRESS_LOout = ~nSP_ADSout ? SP_out : 8'bz;  // DriverInvSel driverinvsel_56
  PullDown #(.Bits(8)) pulldown_75 (.out(DATA_out));
  LED u_D2 (.in(D3));
  LED u_D3 (.in(D4));
  LED A10 (.in(ADDRESS_HIin[2]));
  LED A11 (.in(ADDRESS_HIin[3]));
  CounterPreset #(.Bits(8)) B (
    .en(~1'b1), .C(or_27_out), .dir(1'b0), .in({DATA_in, D6, D5, D4, D3, D2, D1}), .ld(~nB_st),
    .clr(BCD_clr), .out(B_out));  // open: ovf
  CounterPreset #(.Bits(8)) C (
    .en(~1'b1), .C(or_28_out), .dir(1'b0), .in({DATA_in, D6, D5, D4, D3, D2, D1}), .ld(~nC_st),
    .clr(BCD_clr), .out(C_out));  // open: ovf
  CounterPreset #(.Bits(8)) D (
    .en(~1'b1), .C(or_29_out), .dir(1'b0), .in({DATA_in, D6, D5, D4, D3, D2, D1}), .ld(~nD_st),
    .clr(BCD_clr), .out(D_out));  // open: ovf
  PullDown #(.Bits(8)) pulldown_76 (.out(ADDRESS_HIout));
  PullDown #(.Bits(8)) pulldown_77 (.out(ADDRESS_LOout));
  LED u_D1 (.in(D2));
  LED A9 (.in(ADDRESS_HIin[1]));
  Register #(.Bits(8)) register_2 (.D(ADDRESS_LOin), .C(CLK2), .en(~nTADD_st), .Q(register_2_q));
  BitExtender #(.inputBits(7), .outputBits(8)) bitextender_1 (.in(REL_q[6:0]), .out(bitextender_1_out));
  BitExtender #(.inputBits(1), .outputBits(8)) bitextender_2 (.in(REL_q[7]), .out(bitextender_2_out));
  Register #(.Bits(8)) register_3 (.D(ADDRESS_HIin), .C(CLK2), .en(~nTADD_st), .Q(register_3_q));
  assign ADDRESS_LOout = ~nBC_ADSout ? B_out : 8'bz;  // DriverInvSel driverinvsel_57
  assign ADDRESS_HIout = ~nBC_ADSout ? C_out : 8'bz;  // DriverInvSel driverinvsel_58
  assign DATA_out = ~nD_DATout ? D_out : 8'bz;  // DriverInvSel driverinvsel_59
  LED D0 (.in(D1));
  LED A8 (.in(ADDRESS_HIin[0]));
  assign DATA_out = ~nB_DATout ? B_out : 8'bz;  // DriverInvSel driverinvsel_60
  assign DATA_out = ~nC_DATout ? C_out : 8'bz;  // DriverInvSel driverinvsel_61
  LED A6 (.in(ADDRESS_LOin[6]));
  LED A7 (.in(ADDRESS_LOin[7]));
  Add #(.Bits(8)) add_1 (.a(register_2_q), .b(bitextender_1_out), .c_i(1'b0), .s(add_1_s), .c_o(add_1_c_o));
  Add #(.Bits(8)) add_2 (.a(register_3_q), .b(bitextender_2_out), .c_i(add_1_c_o), .s(add_2_s));  // open: c_o
  LED Y (.in(Y_FTdat));
  LED A5 (.in(ADDRESS_LOin[5]));
  assign ADDRESS_LOout = ~nADD_ADSout ? add_1_s : 8'bz;  // DriverInvSel driverinvsel_62
  assign ADDRESS_LOout = ~nPC_ADSout ? PCL_out : 8'bz;  // DriverInvSel driverinvsel_63
  assign DATA_out = ~nPCL_DATout ? PCL_out : 8'bz;  // DriverInvSel driverinvsel_64
  assign ADDRESS_HIout = ~nPC_ADSout ? PCH_out : 8'bz;  // DriverInvSel driverinvsel_65
  assign DATA_out = ~nPCH_DATout ? PCH_out : 8'bz;  // DriverInvSel driverinvsel_66
  PullDown #(.Bits(8)) pulldown_78 (.out(DATA_out));
  PullDown #(.Bits(8)) pulldown_79 (.out(ADDRESS_LOout));
  PullDown #(.Bits(8)) pulldown_80 (.out(DATA_out));
  PullDown #(.Bits(8)) pulldown_81 (.out(ADDRESS_HIout));
  PullDown #(.Bits(8)) pulldown_82 (.out(DATA_out));
  LED X (.in(X_FTdat));
  LED A4 (.in(ADDRESS_LOin[4]));
  PullDown #(.Bits(8)) pulldown_83 (.out(ADDRESS_LOout));
  assign ADDRESS_HIout = ~nADD_ADSout ? add_2_s : 8'bz;  // DriverInvSel driverinvsel_67
  PullDown #(.Bits(8)) pulldown_84 (.out(ADDRESS_HIout));
  PullDown #(.Bits(8)) pulldown_85 (.out(DATA_out));
  PullDown #(.Bits(8)) pulldown_86 (.out(ADDRESS_LOout));
  PullDown #(.Bits(8)) pulldown_87 (.out(DATA_out));
  PullDown #(.Bits(8)) pulldown_88 (.out(ADDRESS_HIout));
  LED V (.in(FLAG_V));
  LED C_2 (.in(FLAG_C));
  LED A2 (.in(ADDRESS_LOin[2]));
  LED A3 (.in(ADDRESS_LOin[3]));
  LED Z (.in(FLAG_NZ[1]));
  LED A1 (.in(ADDRESS_LOin[1]));
  LED N (.in(FLAG_NZ[0]));
  LED A0 (.in(ADDRESS_LOin[0]));

  // Other names for the same wires on the sheet: CLK_1 = CLK1; CLK_2 = CLK2; DATA_in[5:0] = {D6, D5, D4, D3, D2, D1};
  //   nMEM_st = nMEM_in; nTREL_st = nTADD_st

  // Notes on the sheet:
  //   Clock: Hz: 10
  //   Control Sequencing
  //   Conditionals/Misc Control
  //   MEM/BUS
  //   contents of rom_1 (hex, n*v repeats v):
  //   0,0,0,0,0,0,0,0,0,0,0,0,0,0,0,0,0,0,0,0,0,0,0,0,0,0,0,0,0,0,0,0,0,0,0,0,0,0,0,0,0,
  //   0,0,0,0,0,0,0,0,0,0,0,0,0,0,0,0,0,0,0,0,0,0,0,0,0,0,0,0,0,0,0,0,0,0,0,0,0,0,0,0,0,
  //   0,0,0,0,0,0,0,0,0,0,0,0,0,0,0,0,0,0,0,0,0,0,0,0,0,0,0,0,0,0,0,0,0,0,0,0,0,0,0,0,0,
  //   0,0,0,0,0,0,0,0,0,0,0,0,0,0,0,0,0,0,0,0,0,0,0,0,0,0,0,0,0,0,0,0,0,0,0,0,0,0,0,0,0,
  //   0,0,0,0,0,0,0,0,0,0,0,0,0,0,0,0,0,0,0,0,0,0,0,0,0,0,0,0,0,0,0,0,0,0,0,0,0,0,0,0,0,
  //   0,0,0,0,0,0,0,0,0,0,0,0,0,0,0,0,0,0,0,0,0,0,0,0,0,0,0,0,0,0,0,0,0,0,0,0,0,0,0,0,0,
  //   0,0,0,0,0,0,0,0,0,0,0,0,0,0,0,0,0,0,0,0,0,0,0,0,0,0,0,0,0,0,0,0,0,0,0,0,0,0,0,0,0,
  //   0,0,0,0,0,0,0,0,0,0,0,0,0,0,0,0,0,0,0,0,0,0,0,0,0,0,0,0,0,0,0,0,0,0,0,0,0,0,0,0,0,
  //   0,0,0,0,0,0,0,0,0,0,0,0,0,0,0,0,0,0,0,0,0,0,0,0,0,0,0,0,0,0,0,0,0,0,0,0,0,0,0,0,0,
  //   0,0,0,0,0,0,0,0,0,0,0,0,0,0,0,0,0,0,0,0,0,0,0,0,0,0,0,0,0,0,0,0,0,0,0,0,0,0,0,0,0,
  //   0,0,0,0,0,0,0,0,0,0,0,0,0,0,0,0,0,0,0,0,0,0,0,0,0,0,0,0,0,0,0,0,0,0,0,0,0,0,0,0,0,
  //   0,0,0,0,0,0,0,0,0,0,0,0,0,0,0,0,0,0,0,0,0,0,0,0,0,0,0,0,0,0,0,0,0,0,0,0,0,0,0,0,0,
  //   0,0,0,0,0,0,0,0,0,0,0,0,0,0,0,0,0,0,0,0,0,0,0,0,0,0,0,0,0,0,0,0,0,0,0,0,0,0,0,0,0,
  //   0,0,0,0,0,0,0,0,0,0,0,0,0,0,0,0,0,0,0,0,0,0,0,0,0,0,0,0,0,0,0,0,0,0,0,0,0,0,0,0,0,
  //   0,0,0,0,0,0,0,0,0,0,0,0,0,0,0,0,0,0,0,0,0,0,0,0,0,0,0,0,0,0,0,0,0,0,0,0,0,0,0,0,0,
  //   0,0,0,0,0,0,0,0,0,0,0,0,0,0,0,0,0,0,0,0,0,0,0,0,0,0,0,0,0,0,0,0,0,0,0,0,0,0,0,0,0,
  //   0,0,0,0,0,0,0,0,0,0,0,0,0,0,0,0,0,0,0,0,0,0,0,0,0,0,0,0,0,0,0,0,0,0,0,0,0,0,0,0,0,
  //   0,0,0,0,0,0,0,0,0,0,0,0,0,0,0,0,0,0,0,0,0,0,0,0,0,0,0,0,0,0,0,0,0,0,0,0,0,0,0,0,0,
  //   0,0,0,0,0,0,0,0,0,0,0,0,0,0,0,0,0,0,0,0,0,0,0,0,0,0,0,0,0,0,0,0,0,0,0,0,0,0,0,0,0,
  //   0,0,0,0,0,0,0,0,0,0,0,0,0,0,0,0,0,0,0,0,0,0,0,0,0,0,0,0,0,0,0,0,0,0,0,0,0,0,0,0,0,
  //   0,0,0,0,0,0,0,0,0,0,0,0,0,0,0,0,0,0,0,0,0,0,0,0,0,0,0,0,0,0,0,0,0,0,0,0,0,0,0,0,0,
  //   0,0,0,0,0,0,0,0,0,0,0,0,0,0,0,0,0,0,0,0,0,0,0,0,0,0,0,0,0,0,0,0,0,0,0,0,0,0,0,0,0,
  //   0,0,0,0,0,0,0,0,0,0,0,0,0,0,0,0,0,0,0,0,0,0,0,0,0,0,0,0,0,0,0,0,0,0,0,0,0,0,0,0,0,
  //   0,0,0,0,0,0,0,0,0,0,0,0,0,0,0,0,0,0,0,0,0,0,0,0,0,0,0,0,0,0,0,0,0,0,0,0,0,0,0,0,0,
  //   0,0,0,0,0,0,0,0,0,0,0,0,0,0,0,0,0,0,0,0,0,0,0,0,0,0,0,0,0,0,0,0,0,0,0,0,0,0,0,0,0,
  //   0,0,0,0,0,0,0,0,0,0,0,0,0,0,0,0,0,0,0,0,0,0,0,0,0,0,0,0,0,0,0,0,0,0,0,0,0,0,0,0,0,
  //   0,0,0,0,0,0,0,0,0,0,0,0,0,0,0,0,0,0,0,0,0,0,0,0,0,0,0,0,0,0,0,0,0,0,0,0,0,0,0,0,0,
  //   0,0,0,0,0,0,0,0,0,0,0,0,0,0,0,0,0,0,0,0,0,0,0,0,0,0,0,0,0,0,0,0,0,0,0,0,0,0,0,0,0,
  //   0,0,0,0,0,0,0,0,0,0,0,0,0,0,0,0,0,0,0,0,0,0,0,0,0,0,0,0,0,0,0,0,0,0,0,0,0,0,0,0,0,
  //   0,0,0,0,0,0,0,0,0,0,0,0,0,0,0,0,0,0,0,0,0,0,0,0,0,0,0,0,0,0,0,0,0,0,0,0,0,0,0,0,0,
  //   0,0,0,0,0,0,0,0,0,0,0,0,0,0,0,0,0,0,0,0,0,0,0,0,0,0,0,0,0,0,0,0,0,0,0,0,0,0,0,0,0,
  //   0,0,0,0,0,0,0,0,0,0,0,0,0,0,0,0,0,0,0,0,0,0,0,0,0,0,0,0,0,0,0,0,0,0,0,0,0,0,0,0,0,
  //   0,0,0,0,0,0,0,0,0,0,0,0,0,0,0,0,0,0,0,0,0,0,0,0,0,0,0,0,0,0,0,0,0,0,0,0,0,0,0,0,0,
  //   0,0,0,0,0,0,0,0,0,0,0,0,0,0,0,0,0,0,0,0,0,0,0,0,0,0,0,0,0,0,0,0,0,0,0,0,0,0,0,0,0,
  //   0,0,0,0,0,0,0,0,0,0,0,0,0,0,0,0,0,0,0,0,0,0,0,0,0,0,0,0,0,0,0,0,0,0,0,0,0,0,0,0,0,
  //   0,0,0,0,0,0,0,0,0,0,0,0,0,0,0,0,0,0,0,0,0,0,0,0,0,0,0,0,0,0,0,0,0,0,0,0,0,0,0,0,0,
  //   0,0,0,0,0,0,0,0,0,0,0,0,0,0,0,0,0,0,0,0,0,0,0,0,0,0,0,0,0,0,0,0,0,0,0,0,0,0,0,0,0,
  //   0,0,0,0,0,0,0,0,0,0,0,0,0,0,0,0,0,0,0,0,0,0,0,0,0,0,0,0,0,0,0,0,0,0,0,0,0,0,0,0,0,
  //   0,0,0,0,0,0,0,0,0,0,0,0,0,0,0,0,0,0,0,0,0,0,0,0,0,0,0,0,0,0,0,0,0,0,0,0,0,0,0,0,0,
  //   0,0,0,0,0,0,0,0,0,0,0,0,0,0,0,0,0,0,0,0,0,0,0,0,0,0,0,0,0,0,0,0,0,0,0,0,0,0,0,0,0,
  //   0,0,0,0,0,0,0,0,0,0,0,0,0,0,0,0,0,0,0,0,0,0,0,0,0,0,0,0,0,0,0,0,0,0,0,0,0,0,0,0,0,
  //   0,0,0,0,0,0,0,0,0,0,0,0,0,0,0,0,0,0,0,0,0,0,0,0,0,0,0,0,0,0,0,0,0,0,0,0,0,0,0,0,0,
  //   0,0,0,0,0,0,0,0,0,0,0,0,0,0,0,0,0,0,0,0,0,0,0,0,0,0,0,0,0,0,0,0,0,0,0,0,0,0,0,0,0,
  //   0,0,0,0,0,0,0,0,0,0,0,0,0,0,0,0,0,0,0,0,0,0,0,0,0,0,0,0,0,0,0,0,0,0,0,0,0,0,0,0,0,
  //   0,0,0,0,0,0,0,0,0,0,0,0,0,0,0,0,0,0,0,0,0,0,0,0,0,0,0,0,0,0,0,0,0,0,0,0,0,0,0,0,0,
  //   0,0,0,0,0,0,0,0,0,0,0,0,0,0,0,0,0,0,0,0,0,0,0,0,0,0,0,0,0,0,0,0,0,0,0,0,0,0,0,0,0,
  //   0,0,0,0,0,0,0,0,0,0,0,0,0,0,0,0,0,0,0,0,0,0,0,0,0,0,0,0,0,0,0,0,0,0,0,0,0,0,0,0,0,
  //   0,0,0,0,0,0,0,0,0,0,0,0,0,0,0,0,0,0,0,0,0,0,0,0,0,0,0,0,0,0,0,0,0,0,0,0,0,0,0,0,0,
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  //   contents of µCODE (hex, n*v repeats v):
  //   12000000a25,2000400009,2800000266,2000000a32,24000b0240,2000000a33,4800001806,0,0,
  //   0,0,0,0,0,0,0,0,0,0,0,0,0,0,0,0,0,0,0,0,0,0,0,30000000000,30000000000,30000000000,
  //   30000000000,30000000000,30000000000,30000000000,30000000000,30000000000,30000000000,
  //   30000000000,30000000000,30000000000,30000000000,30000000000,30000000000,30000000000,
  //   30000000000,30000000000,30000000000,30000000000,30000000000,30000000000,30000000000,
  //   30000000000,30000000000,30000000000,30000000000,30000000000,30000000000,30000000000,
  //   30000000000,12000000a25,2000400009,2800000266,2000000a32,24000b0240,2000000a33,4800001806,
  //   0,0,0,0,0,0,0,0,0,0,0,0,0,0,0,0,0,0,0,0,0,0,0,0,0,30000000000,30000000000,30000000000,
  //   30000000000,30000000000,30000000000,30000000000,30000000000,30000000000,30000000000,
  //   30000000000,30000000000,30000000000,30000000000,30000000000,30000000000,30000000000,
  //   30000000000,30000000000,30000000000,30000000000,30000000000,30000000000,30000000000,
  //   30000000000,30000000000,30000000000,30000000000,30000000000,30000000000,30000000000,
  //   30000000000,12000000a25,2000400009,2800000266,2000000a32,24000b0240,2000000a33,4800001806,
  //   0,0,0,0,0,0,0,0,0,0,0,0,0,0,0,0,0,0,0,0,0,0,0,0,0,30000000000,30000000000,30000000000,
  //   30000000000,30000000000,30000000000,30000000000,30000000000,30000000000,30000000000,
  //   30000000000,30000000000,30000000000,30000000000,30000000000,30000000000,30000000000,
  //   30000000000,30000000000,30000000000,30000000000,30000000000,30000000000,30000000000,
  //   30000000000,30000000000,30000000000,30000000000,30000000000,30000000000,30000000000,
  //   30000000000,12000000a25,2000400009,2800000266,2000000a32,24000b0240,2000000a33,4800001806,
  //   0,0,0,0,0,0,0,0,0,0,0,0,0,0,0,0,0,0,0,0,0,0,0,0,0,30000000000,30000000000,30000000000,
  //   30000000000,30000000000,30000000000,30000000000,30000000000,30000000000,30000000000,
  //   30000000000,30000000000,30000000000,30000000000,30000000000,30000000000,30000000000,
  //   30000000000,30000000000,30000000000,30000000000,30000000000,30000000000,30000000000,
  //   30000000000,30000000000,30000000000,30000000000,30000000000,30000000000,30000000000,
  //   30000000000,12000000a25,2000400009,2800000266,2000000a32,24000b0240,2000000a33,4800001806,
  //   0,0,0,0,0,0,0,0,0,0,0,0,0,0,0,0,0,0,0,0,0,0,0,0,0,30000000000,30000000000,30000000000,
  //   30000000000,30000000000,30000000000,30000000000,30000000000,30000000000,30000000000,
  //   30000000000,30000000000,30000000000,30000000000,30000000000,30000000000,30000000000,
  //   30000000000,30000000000,30000000000,30000000000,30000000000,30000000000,30000000000,
  //   30000000000,30000000000,30000000000,30000000000,30000000000,30000000000,30000000000,
  //   30000000000,12000000a25,2000400009,2800000266,2000000a32,24000b0240,2000000a33,4800001806,
  //   0,0,0,0,0,0,0,0,0,0,0,0,0,0,0,0,0,0,0,0,0,0,0,0,0,30000000000,30000000000,30000000000,
  //   30000000000,30000000000,30000000000,30000000000,30000000000,30000000000,30000000000,
  //   30000000000,30000000000,30000000000,30000000000,30000000000,30000000000,30000000000,
  //   30000000000,30000000000,30000000000,30000000000,30000000000,30000000000,30000000000,
  //   30000000000,30000000000,30000000000,30000000000,30000000000,30000000000,30000000000,
  //   30000000000,12000000a25,2000400009,2800000266,2000000a32,24000b0240,2000000a33,4800001806,
  //   0,0,0,0,0,0,0,0,0,0,0,0,0,0,0,0,0,0,0,0,0,0,0,0,0,30000000000,30000000000,30000000000,
  //   30000000000,30000000000,30000000000,30000000000,30000000000,30000000000,30000000000,
  //   30000000000,30000000000,30000000000,30000000000,30000000000,30000000000,30000000000,
  //   30000000000,30000000000,30000000000,30000000000,30000000000,30000000000,30000000000,
  //   30000000000,30000000000,30000000000,30000000000,30000000000,30000000000,30000000000,
  //   30000000000,12000000a25,2000400009,2800000266,2000000a32,24000b0240,2000000a33,4800001806,
  //   0,0,0,0,0,0,0,0,0,0,0,0,0,0,0,0,0,0,0,0,0,0,0,0,0,30000000000,30000000000,30000000000,
  //   30000000000,30000000000,30000000000,30000000000,30000000000,30000000000,30000000000,
  //   30000000000,30000000000,30000000000,30000000000,30000000000,30000000000,30000000000,
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  //   ALU/PC
  //   ALU
  //   FRONT PANEL
  //   ATLAS CPU-8
  //   By Hayden B.
endmodule
