// Digital circuit CopyPaste.dig as structural Verilog
module CopyPaste (
  input  clk,
  input  nST,
  input  nEN,
  output out_1,
  output [15:0] out_5
);

  wire and_1_out, and_2_out, and_3_out, and_4_out, and_5_out, and_6_out, and_7_out, CLK_2,
       demultiplexer_1_out_0, demultiplexer_1_out_1, HLT, IRQ_0, IRQ_VECT_any, keyboard_1_av, nIR_st,
       nIRQ_ack, nIRQ_en, nor_1_out, not_1_out, not_3_out, not_4_out, not_5_out, not_6_out, not_7_out,
       not_8_out, not_9_out, nRST, nRST_SEQen, nSTAT_st, or_1_out, REG_aop, RESET_out, RST_ack, RST_IRen,
       SP_sel, TMP_clr;
  wire [2:0] IR_q, IR_q_2, IRQ_VECT_num, multiplexer_1_out, REG_ADS;
  wire [6:0] MASK;
  wire [7:0] keyboard_1_d;
  wire [15:0] DATA, driverinvsel_2_out;
  wire [15:6] IR_q_3;
  wire [15:8] keyboard_1_d_2;

  Register #(.Bits(7)) u_MASK (.D(DATA[14:8]), .C(CLK_2), .en(~nSTAT_st), .Q(MASK));
  not not_1 (not_1_out, 1'b1);
  and and_1 (and_1_out, MASK[0], ~IRQ_0);  // And
  and and_2 (and_2_out, MASK[1], ~1'b1);  // And
  and and_3 (and_3_out, MASK[2], ~1'b1);  // And
  and and_4 (and_4_out, MASK[3], ~1'b1);  // And
  and and_5 (and_5_out, MASK[4], ~1'b1);  // And
  and and_6 (and_6_out, MASK[5], ~1'b1);  // And
  and and_7 (and_7_out, MASK[6], ~1'b1);  // And
  PriorityEncoder #(.Selector_Bits(3)) IRQ_VECT (
    .in0(not_1_out), .in1(and_1_out), .in2(and_2_out), .in3(and_3_out), .in4(and_4_out), .in5(and_5_out),
    .in6(and_6_out), .in7(and_7_out), .num(IRQ_VECT_num), .any(IRQ_VECT_any));
  PriorityEncoder #(.Selector_Bits(3)) FAULT_VECT (
    .in0(1'b0), .in1(1'b0), .in2(1'b0), .in3(1'b0), .in4(1'b0), .in5(1'b0), .in6(1'b0), .in7(1'b0));  // open: num, any
  assign DATA = ~or_1_out ? {{13{1'b0}}, IRQ_VECT_num} : 16'bz;  // DriverInvSel driverinvsel_1
  PullDown #(.Bits(16)) pulldown_1 (.out(DATA));
  or or_1 (or_1_out, ~IRQ_VECT_any, nIRQ_ack);  // Or
  assign driverinvsel_2_out = ~1'b1 ? DATA : 16'bz;  // DriverInvSel driverinvsel_2
  PullUp pullup_1 (.out(HLT));
  PullDown #(.Bits(16)) pulldown_2 (.out(driverinvsel_2_out));
  Register #(.Bits(16)) IR (.D(driverinvsel_2_out), .C(CLK_2), .en(~nIR_st), .Q({IR_q_3, IR_q_2, IR_q}));
  nor nor_1 (nor_1_out, HLT, RST_IRen);
  Register u_HLT (.D(nor_1_out), .C(CLK_2), .en(~1'b0), .Q(out_5[4]));
  Register IRQ (.D(IRQ_VECT_any), .C(CLK_2), .en(~nIRQ_en), .Q(out_5[5]));
  Multiplexer #(.Bits(3)) multiplexer_1 (.sel(REG_aop), .in_0(IR_q_2), .in_1(IR_q), .out(multiplexer_1_out));
  Multiplexer #(.Bits(3)) multiplexer_2 (.sel(SP_sel), .in_0(multiplexer_1_out), .in_1(3'b111), .out(REG_ADS));
  // Probe on 10'h1
  not not_2 (nRST, RESET_out);
  DipSwitch RESET (.out(RESET_out));
  not not_3 (not_3_out, TMP_clr);
  not not_4 (not_4_out, RST_ack);
  // _7474 _7474_1: pin names not known; wires that end beside it: nRST, 1'b0, 1'b0, not_3_out, nRST, 1'b0, 1'b0, not_4_out, 1'b1, 1'b0, nRST_SEQen, RST_IRen
  Demultiplexer demultiplexer_1 (
    .sel(nST), .in(not_5_out), .out_0(demultiplexer_1_out_0), .out_1(demultiplexer_1_out_1));
  not not_5 (not_5_out, nEN);
  not not_6 (not_6_out, demultiplexer_1_out_0);
  not not_7 (not_7_out, demultiplexer_1_out_1);
  Terminal #(.termWidth(80), .termHeight(24)) terminal_1 (.D(keyboard_1_d), .C(clk), .en(not_8_out));
  not not_8 (not_8_out, not_6_out);
  Keyboard keyboard_1 (.C(clk), .en(not_9_out), .D({keyboard_1_d_2, keyboard_1_d}), .av(keyboard_1_av));
  not not_9 (not_9_out, not_7_out);
  not not_10 (out_1, keyboard_1_av);

  assign {out_5[15:6], out_5[3:0]} = 14'h11;

  // Notes on the sheet:
  //   nEN: default 1
endmodule
