// Digital circuit MEMORY MAP STATE.dig as structural Verilog
module MEMORY_MAP_STATE (
  input  [15:0] A,
  input  WR,
  input  [1:0] MD,
  input  EN,
  output Q4,
  output Q3,
  output Q2,
  output Q1,
  output Q0
);

  wire and_1_out, and_2_out, comparator_1_lt, comparator_2_gt, comparator_3_lt, comparator_4_gt,
       comparator_5_lt, comparator_6_gt, comparator_7_lt, comparator_8_gt, comparator_9_lt, comparator_10_gt,
       comparator_11_lt, comparator_12_eq, comparator_13_eq, driverinvsel_1_out, driverinvsel_2_out,
       driverinvsel_3_out, driverinvsel_4_out, driverinvsel_5_out, driverinvsel_6_out, multiplexer_1_out,
       multiplexer_2_out, multiplexer_3_out, not_1_out, or_1_out, or_2_out, or_3_out, or_4_out;
  wire [2:2] not_2_out;

  Comparator #(.Bits(16)) comparator_1 (.a(A), .b(16'hbb80), .lt(comparator_1_lt));  // open: gt, eq
  Comparator #(.Bits(16)) comparator_2 (.a(A), .b(16'hbb79), .gt(comparator_2_gt));  // open: eq, lt
  Comparator #(.Bits(16)) comparator_3 (.a(A), .b(16'hdac0), .lt(comparator_3_lt));  // open: gt, eq
  Comparator #(.Bits(16)) comparator_4 (.a(A), .b(16'hdabf), .gt(comparator_4_gt));  // open: eq, lt
  Comparator #(.Bits(16)) comparator_5 (.a(A), .b(16'hdac0), .lt(comparator_5_lt));  // open: gt, eq
  Comparator #(.Bits(16)) comparator_6 (.a(A), .b(16'hdabf), .gt(comparator_6_gt));  // open: eq, lt
  Comparator #(.Bits(16)) comparator_7 (.a(A), .b(16'hbb80), .lt(comparator_7_lt));  // open: gt, eq
  Comparator #(.Bits(16)) comparator_8 (.a(A), .b(16'hbb79), .gt(comparator_8_gt));  // open: eq, lt
  Comparator #(.Bits(16)) comparator_9 (.a(A), .b(16'hdac0), .lt(comparator_9_lt));  // open: gt, eq
  Comparator #(.Bits(16)) comparator_10 (.a(A), .b(16'hdabf), .gt(comparator_10_gt));  // open: eq, lt
  Comparator #(.Bits(16)) comparator_11 (.a(A), .b({16{1'b0}}), .lt(comparator_11_lt));  // open: gt, eq
  not not_1 (not_1_out, comparator_11_lt);
  and and_1 (and_1_out, comparator_2_gt, comparator_3_lt);
  and and_2 (and_2_out, comparator_8_gt, comparator_9_lt);
  or or_1 (or_1_out, comparator_1_lt, comparator_4_gt);
  or or_2 (or_2_out, comparator_6_gt, comparator_5_lt);
  or or_3 (or_3_out, comparator_7_lt, comparator_10_gt);
  not not_2 (not_2_out[2], WR);
  Multiplexer #(.Selector_Bits(3)) multiplexer_1 (
    .sel({not_2_out[2], MD}), .in_0(comparator_1_lt), .in_1(comparator_5_lt), .in_2(or_3_out),
    .in_3(not_1_out), .in_4(or_1_out), .in_5(or_2_out), .in_6(or_3_out), .in_7(not_1_out),
    .out(multiplexer_1_out));
  Multiplexer #(.Selector_Bits(3)) multiplexer_2 (
    .sel({not_2_out[2], MD}), .in_0(comparator_4_gt), .in_1(comparator_6_gt), .in_2(1'b0), .in_3(1'b0),
    .in_4(1'b0), .in_5(1'b0), .in_6(1'b0), .in_7(1'b0), .out(multiplexer_2_out));
  Multiplexer #(.Selector_Bits(3)) multiplexer_3 (
    .sel({not_2_out[2], MD}), .in_0(and_1_out), .in_1(1'b0), .in_2(and_2_out), .in_3(1'b0), .in_4(and_1_out),
    .in_5(1'b0), .in_6(and_2_out), .in_7(1'b0), .out(multiplexer_3_out));
  Comparator #(.Bits(16)) comparator_12 (.a(A), .b(16'h4), .eq(comparator_12_eq));  // open: gt, lt
  Comparator #(.Bits(16)) comparator_13 (.a(A), .b(16'h5), .eq(comparator_13_eq));  // open: gt, lt
  or or_4 (or_4_out, comparator_12_eq, comparator_13_eq);
  assign driverinvsel_1_out = ~or_4_out ? multiplexer_1_out : 1'bz;  // DriverInvSel driverinvsel_1
  PullDown pulldown_1 (.out(driverinvsel_1_out));
  assign driverinvsel_2_out = ~EN ? comparator_12_eq : 1'bz;  // DriverInvSel driverinvsel_2
  assign driverinvsel_3_out = ~EN ? multiplexer_2_out : 1'bz;  // DriverInvSel driverinvsel_3
  assign driverinvsel_4_out = ~EN ? multiplexer_3_out : 1'bz;  // DriverInvSel driverinvsel_4
  assign driverinvsel_5_out = ~EN ? driverinvsel_1_out : 1'bz;  // DriverInvSel driverinvsel_5
  assign driverinvsel_6_out = ~EN ? comparator_13_eq : 1'bz;  // DriverInvSel driverinvsel_6
  PullDown pulldown_2 (.out(driverinvsel_2_out));
  not not_3 (Q3, driverinvsel_2_out);
  PullDown pulldown_3 (.out(driverinvsel_5_out));
  not not_4 (Q0, driverinvsel_5_out);
  not not_5 (Q4, driverinvsel_6_out);
  PullDown pulldown_4 (.out(driverinvsel_6_out));
  PullDown pulldown_5 (.out(driverinvsel_3_out));
  not not_6 (Q1, driverinvsel_3_out);
  PullDown pulldown_6 (.out(driverinvsel_4_out));
  not not_7 (Q2, driverinvsel_4_out);
endmodule
