// Digital circuit PAGING.dig as structural Verilog
module PAGING (
);

  wire and_1_out, and_2_out, and_3_out, and_4_out, and_5_out, CLK_2, demultiplexer_1_out_0,
       demultiplexer_1_out_1, demultiplexer_1_out_2, demultiplexer_1_out_3, demultiplexer_1_out_4,
       nMEM_DATout, nMEM_en, nMEM_HIin, nMEM_LOin, nMEM_st, nOMEM_st, not_1_out, not_2_out, not_3_out,
       not_4_out, not_5_out, not_6_out, not_7_out, nPTB_sel, nTMEM_st, or_1_out, or_2_out, PTB_clr, TEMP_clr;
  wire [2:0] PAGE_sel2, PAGE_sel3;
  wire [6:0] PAGE_sel;
  wire [7:0] ADDRESS_HIin, ADDRESS_LOin, TMEM_out, TMEM_out_2;
  wire [7:5] PAGE1_d;
  wire [15:0] DATA_in, DATA_out;
  wire [17:5] undriven;

  CounterPreset #(.Bits(8)) PTB (
    .en(~1'b1), .C(CLK_2), .dir(1'b0), .in(DATA_in[7:0]), .ld(~nPTB_sel), .clr(PTB_clr), .out(undriven[14:7]));  // open: ovf
  RAMSinglePortSel #(.AddrBits(18), .Bits(8)) PAGE0 (
    .A({undriven, ADDRESS_HIin[7:3]}), .D({PAGE_sel2[0], PAGE_sel}));  // open: CS, WE, OE
  RAMSinglePortSel #(.AddrBits(18), .Bits(8)) PAGE1 (
    .A({undriven, ADDRESS_HIin[7:3]}), .D({PAGE1_d, PAGE_sel3, PAGE_sel2[2:1]}));  // open: CS, WE, OE
  or or_1 (or_1_out, PAGE_sel3[1], PAGE_sel3[2]);
  or or_2 (or_2_out, PAGE_sel3[0], or_1_out);
  not not_1 (not_1_out, or_2_out);
  Demultiplexer #(.Selector_Bits(3)) demultiplexer_1 (
    .sel(PAGE_sel2), .in(not_1_out), .out_0(demultiplexer_1_out_0), .out_1(demultiplexer_1_out_1),
    .out_2(demultiplexer_1_out_2), .out_3(demultiplexer_1_out_3), .out_4(demultiplexer_1_out_4));  // open: out_5, out_6, out_7
  not not_2 (not_2_out, demultiplexer_1_out_0);
  not not_3 (not_3_out, demultiplexer_1_out_1);
  not not_4 (not_4_out, demultiplexer_1_out_2);
  not not_5 (not_5_out, demultiplexer_1_out_3);
  not not_6 (not_6_out, demultiplexer_1_out_4);
  and and_1 (and_1_out, not_2_out, nMEM_en);
  and and_2 (and_2_out, not_3_out, nMEM_en);
  and and_3 (and_3_out, not_4_out, nMEM_en);
  and and_4 (and_4_out, not_5_out, nMEM_en);
  and and_5 (and_5_out, not_6_out, nMEM_en);
  not not_7 (not_7_out, and_1_out);
  ROM #(.AddrBits(18), .Bits(8)) ROM__256K (
    .A({PAGE_sel, ADDRESS_HIin[2:0], ADDRESS_LOin}), .sel(not_7_out), .D(DATA_out[15:8]));
  RAMSinglePortSel #(.AddrBits(18), .Bits(8)) RAM0__256K (
    .A({PAGE_sel, ADDRESS_HIin[2:0], ADDRESS_LOin}), .CS(~and_2_out), .WE(~nMEM_st), .OE(~nMEM_DATout),
    .D(DATA_out[15:8]));
  RAMSinglePortSel #(.AddrBits(18), .Bits(8)) RAM1__256K (
    .A({PAGE_sel, ADDRESS_HIin[2:0], ADDRESS_LOin}), .CS(~and_3_out), .WE(~nMEM_st), .OE(~nMEM_DATout),
    .D(DATA_out[15:8]));
  RAMSinglePortSel #(.AddrBits(18), .Bits(8)) RAM2__256K (
    .A({PAGE_sel, ADDRESS_HIin[2:0], ADDRESS_LOin}), .CS(~and_4_out), .WE(~nMEM_st), .OE(~nMEM_DATout),
    .D(DATA_out[15:8]));
  RAMSinglePortSel #(.AddrBits(18), .Bits(8)) RAM3__256K (
    .A({PAGE_sel, ADDRESS_HIin[2:0], ADDRESS_LOin}), .CS(~and_5_out), .WE(~nMEM_st), .OE(~nMEM_DATout),
    .D(DATA_out[15:8]));
  assign DATA_out[15:8] = ~nMEM_HIin ? TMEM_out_2 : 8'bz;  // DriverInvSel driverinvsel_1
  assign DATA_out[15:8] = ~nMEM_LOin ? TMEM_out : 8'bz;  // DriverInvSel driverinvsel_2
  CounterPreset #(.Bits(8)) OMEM (
    .en(~1'b1), .C(CLK_2), .dir(1'b0), .in(DATA_out[15:8]), .ld(~nOMEM_st), .clr(TEMP_clr),
    .out(DATA_out[7:0]));  // open: ovf
  CounterPreset #(.Bits(16)) TMEM (
    .en(~1'b1), .C(CLK_2), .dir(1'b0), .in(DATA_in), .ld(~nTMEM_st), .clr(TEMP_clr),
    .out({TMEM_out_2, TMEM_out}));  // open: ovf
  // Pins of 8 and 16 bits meet at DATA_in
  // Pins of 16 and 18 bits meet at {undriven, ADDRESS_HIin[7:3]}
  // Pins of 5 and 7 bits meet at {undriven[6:5], ADDRESS_HIin[7:3]}

  // Other names for the same wires on the sheet: PAGE_off[10:0] = {ADDRESS_HIin[2:0], ADDRESS_LOin}

  // Notes on the sheet:
  //   contents of ROM__256K (hex, n*v repeats v):
  //   0,0,0,0,0,0,0,0,0,0,0,0,0,0,0,0,0,0,0,0,0,0,0,0,0,0,0,0,0,0,0,0,0,0,0,0,0,0,0,0,0,
  //   0,0,0,0,0,0,0,0,0,0,0,0,0,0,0,0,0,0,0,0,0,0,0,0,0,0,0,0,0,0,0,0,0,0,0,0,0,0,0,0,0,
  //   0,0,0,0,0,0,0,0,0,0,0,0,0,0,0,0,0,0,0,0,0,0,0,0,0,0,0,0,0,0,0,0,0,0,0,0,0,0,0,0,0,
  //   0,0,0,0,0,0,0,0,0,0,0,0,0,0,0,0,0,0,0,0,0,0,0,0,0,0,0,0,0,0,0,0,0,0,0,0,0,0,0,0,0,
  //   0,0,0,0,0,0,0,0,0,0,0,0,0,0,0,0,0,0,0,0,0,0,0,0,0,0,0,0,0,0,0,0,0,0,0,0,0,0,0,0,0,
  //   0,0,0,0,0,0,0,0,0,0,0,0,0,0,0,0,0,0,0,0,0,0,0,0,0,0,0,0,0,0,0,0,0,0,0,0,0,0,0,0,0,
  //   0,0,0,0,0,0,0,0,0,0,0,0,0,0,0,0,0,0,0,0,0,0,0,0,0,0,0,0,0,0,0,0,0,0,0,0,0,0,0,0,0,
  //   0,0,0,0,0,0,0,0,0,0,0,0,0,0,0,0,0,0,0,0,0,0,0,0,0,0,0,0,0,0,0,0,0,0,0,0,0,0,0,0,0,
  //   0,0,0,0,0,0,0,0,0,0,0,0,0,0,0,0,0,0,0,0,0,0,0,0,0,0,0,0,0,0,0,0,0,0,0,0,0,0,0,0,0,
  //   0,0,0,0,0,0,0,0,0,0,0,0,0,0,0,0,0,0,0,0,0,0,0,0,0,0,0,0,0,0,0,0,0,0,0,0,0,0,0,0,0,
  //   0,0,0,0,0,0,0,0,0,0,0,0,0,0,0,0,0,0,0,0,0,0,0,0,0,0,0,0,0,0,0,0,0,0,0,0,0,0,0,0,0,
  //   0,0,0,0,0,0,0,0,0,0,0,0,0,0,0,0,0,0,0,0,0,0,0,0,0,0,0,0,0,0,0,0,0,0,0,0,0,0,0,0,0,
  //   0,0,0,0,0,0,0,0,0,0,0,0,0,0,0,0,0,0,0,0,0,0,0,0,0,0,0,0,0,0,0,0,0,0,0,0,0,0,0,0,0,
  //   0,0,0,0,0,0,0,0,0,0,0,0,0,0,0,0,0,0,0,0,0,0,0,0,0,0,0,0,0,0,0,0,0,0,0,0,0,0,0,0,0,
  //   0,0,0,0,0,0,0,0,0,0,0,0,0,0,0,0,0,0,0,0,0,0,0,0,0,0,0,0,0,0,0,0,0,0,0,0,0,0,0,0,0,
  //   0,0,0,0,0,0,0,0,0,0,0,0,0,0,0,0,0,0,0,0,0,0,0,0,0,0,0,0,0,0,0,0,0,0,0,0,0,0,0,0,0,
  //   0,0,0,0,0,0,0,0,0,0,0,0,0,0,0,0,0,0,0,0,0,0,0,0,0,0,0,0,0,0,0,0,0,0,0,0,0,0,0,0,0,
  //   0,0,0,0,0,0,0,0,0,0,0,0,0,0,0,0,0,0,0,0,0,0,0,0,0,0,0,0,0,0,0,0,0,0,0,0,0,0,0,0,0,
  //   0,0,0,0,0,0,0,0,0,0,0,0,0,0,0,0,0,0,0,0,0,0,0,0,0,0,0,0,0,0,0,0,0,0,0,0,0,0,0,0,0,
  //   0,0,0,0,0,0,0,0,0,0,0,0,0,0,0,0,0,0,0,0,0,0,0,0,0,0,0,0,0,0,0,0,0,0,0,0,0,0,0,0,0,
  //   0,0,0,0,0,0,0,0,0,0,0,0,0,0,0,0,0,0,0,0,0,0,0,0,0,0,0,0,0,0,0,0,0,0,0,0,0,0,0,0,0,
  //   0,0,0,0,0,0,0,0,0,0,0,0,0,0,0,0,0,0,0,0,0,0,0,0,0,0,0,0,0,0,0,0,0,0,0,0,0,0,0,0,0,
  //   0,0,0,0,0,0,0,0,0,0,0,0,0,0,0,0,0,0,0,0,0,0,0,0,0,0,0,0,0,0,0,0,0,0,0,0,0,0,0,0,0,
  //   0,0,0,0,0,0,0,0,0,0,0,0,0,0,0,0,0,0,0,0,0,0,0,0,0,0,0,0,0,0,0,0,0,0,0,0,0,0,0,0,0,
  //   0,0,0,0,0,0,0,0,0,0,0,0,0,0,0,0,0,0,0,0,0,0,0,0,0,0,0,0,0,0,0,0,0,0,0,0,0,0,0,0,0,
  //   0,0,0,0,0,0,0,0,0,0,0,0,0,0,0,0,0,0,0,0,0,0,0,0,0,0,0,0,0,0,0,0,0,0,0,0,0,0,0,0,0,
  //   0,0,0,0,0,0,0,0,0,0,0,0,0,0,0,0,0,0,0,0,0,0,0,0,0,0,0,0,0,0,0,0,0,0,0,0,0,0,0,0,0,
  //   0,0,0,0,0,0,0,0,0,0,0,0,0,0,0,0,0,0,0,0,0,0,0,0,0,0,0,0,0,0,0,0,0,0,0,0,0,0,0,0,0,
  //   0,0,0,0,0,0,0,0,0,0,0,0,0,0,0,0,0,0,0,0,0,0,0,0,0,0,0,0,0,0,0,0,0,0,0,0,0,0,0,0,0,
  //   0,0,0,0,0,0,0,0,0,0,0,0,0,0,0,0,0,0,0,0,0,0,0,0,0,0,0,0,0,0,0,0,0,0,0,0,0,0,0,0,0,
  //   0,0,0,0,0,0,0,0,0,0,0,0,0,0,0,0,0,0,0,0,0,0,0,0,0,0,0,0,0,0,0,0,0,0,0,0,0,0,0,0,0,
  //   0,0,0,0,0,0,0,0,0,0,0,0,0,0,0,0,0,0,0,0,0,0,0,0,0,0,0,0,0,0,0,0,0,0,0,0,0,0,0,0,0,
  //   0,0,0,0,0,0,0,0,0,0,0,0,0,0,0,0,0,0,0,0,0,0,0,0,0,0,0,0,0,0,0,0,0,0,0,0,0,0,0,0,0,
  //   0,0,0,0,0,0,0,0,0,0,0,0,0,0,0,0,0,0,0,0,0,0,0,0,0,0,0,0,0,0,0,0,0,0,0,0,0,0,0,0,0,
  //   0,0,0,0,0,0,0,0,0,0,0,0,0,0,0,0,0,0,0,0,0,0,0,0,0,0,0,0,0,0,0,0,0,0,0,0,0,0,0,0,0,
  //   0,0,0,0,0,0,0,0,0,0,0,0,0,0,0,0,0,0,0,0,0,0,0,0,0,0,0,0,0,0,0,0,0,0,0,0,0,0,0,0,0,
  //   0,0,0,0,0,0,0,0,0,0,0,0,0,0,0,0,0,0,0,0,0,0,0,0,0,0,0,0,0,0,0,0,0,0,0,0,0,0,0,0,0,
  //   0,0,0,0,0,0,0,0,0,0,0,0,0,0,0,0,0,0,0,0,0,0,0,0,0,0,0,0,0,0,0,0,0,0,0,0,0,0,0,0,0,
  //   0,0,0,0,0,0,0,0,0,0,0,0,0,0,0,0,0,0,0,0,0,0,0,0,0,0,0,0,0,0,0,0,0,0,0,0,0,0,0,0,0,
  //   0,0,0,0,0,0,0,0,0,0,0,0,0,0,0,0,0,0,0,0,0,0,0,0,0,0,0,0,0,0,0,0,0,0,0,0,0,0,0,0,0,
  //   0,0,0,0,0,0,0,0,0,0,0,0,0,0,0,0,0,0,0,0,0,0,0,0,0,0,0,0,0,0,0,0,0,0,0,0,0,0,0,0,0,
  //   0,0,0,0,0,0,0,0,0,0,0,0,0,0,0,0,0,0,0,0,0,0,0,0,0,0,0,0,0,0,0,0,0,0,0,0,0,0,0,0,0,
  //   0,0,0,0,0,0,0,0,0,0,0,0,0,0,0,0,0,0,0,0,0,0,0,0,0,0,0,0,0,0,0,0,0,0,0,0,0,0,0,0,0,
  //   0,0,0,0,0,0,0,0,0,0,0,0,0,0,0,0,0,0,0,0,0,0,0,0,0,0,0,0,0,0,0,0,0,0,0,0,0,0,0,0,0,
  //   0,0,0,0,0,0,0,0,0,0,0,0,0,0,0,0,0,0,0,0,0,0,0,0,0,0,0,0,0,0,0,0,0,0,0,0,0,0,0,0,0,
  //   0,0,0,0,0,0,0,0,0,0,0,0,0,0,0,0,0,0,0,0,0,0,0,0,0,0,0,0,0,0,0,0,0,0,0,0,0,0,0,0,0,
  //   0,0,0,0,0,0,0,0,0,0,0,0,0,0,0,0,0,0,0,0,0,0,0,0,0,0,0,0,0,0,0,0,0,0,0,0,0,0,0,0,0,
  //   0,0,0,0,0,0,0,0,0,0,0,0,0,0,0,0,0,0,0,0,0,0,0,0,0,0,0,0,0,0,0,0,0,0,0,0,0,0,0,0,0,
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endmodule
