// Digital circuit Testing.dig as structural Verilog
module Testing (
  input  in_1,
  input  in_4,
  input  in_5,
  input  in_6,
  input  in_7,
  input  in_8,
  input  in_9,
  input  in_10,
  input  in_11,
  input  in_13,
  input  in_14,
  input  in_15,
  input  in_16,
  input  in_25,
  input  in_34,
  input  in_35,
  input  in_36,
  input  in_37,
  input  in_38,
  input  in_39,
  input  in_40,
  input  in_41,
  input  in_42,
  input  in_43,
  input  in_44,
  input  in_45,
  input  in_46,
  input  in_47,
  input  in_48,
  input  in_49,
  input  in_50,
  input  in_51,
  input  in_52,
  input  in_61,
  input  in_62,
  input  in_63,
  input  C,
  input  C_en,
  input  in_66,
  input  E,
  input  E_en,
  input  in_70,
  input  in_71,
  input  in_74,
  input  in_75,
  input  in_76,
  input  in_77,
  input  in_79,
  input  in_80,
  input  [7:0] in_82,
  input  [7:0] in_83,
  input  Ci,
  input  nmemst,
  input  nsel,
  input  nmemst_2,
  input  nsel_2,
  input  in_93,
  input  in_94,
  input  in_95,
  input  in_97,
  input  in_98,
  input  in_102,
  input  in_103,
  input  in_104,
  input  in_105,
  input  in_106,
  input  in_107,
  input  in_108,
  input  in_109,
  input  in_110,
  input  in_111,
  input  in_112,
  input  in_113,
  input  in_114,
  input  in_115,
  input  in_116,
  input  in_117,
  input  in_118,
  input  in_119,
  input  in_120,
  input  in_121,
  input  in_122,
  input  in_123,
  input  in_124,
  input  in_125,
  input  in_128,
  input  in_129,
  input  clk,
  input  in_132,
  input  in_133,
  output out_2,
  output out_3,
  output out_12,
  output out_17,
  output out_18,
  output out_19,
  output out_20,
  output out_21,
  output out_22,
  output out_23,
  output out_24,
  output out_26,
  output out_27,
  output out_28,
  output out_29,
  output out_30,
  output out_31,
  output out_32,
  output out_33,
  output out_53,
  output out_54,
  output out_55,
  output out_56,
  output out_57,
  output out_58,
  output out_59,
  output out_60,
  output out_67,
  output out_72,
  output out_73,
  output out_78,
  output out_81,
  output [7:0] out_85,
  output out_86,
  output out_87,
  output out_90,
  output out_96,
  output out_99,
  output [2:0] out_100,
  output out_101,
  output [2:0] out_126,
  output out_127,
  output out_130,
  output out_134
);

  wire and_3_out, and_4_out, and_6_out, and_7_out, and_9_out, and_10_out, and_12_out, driver_1_out,
       driver_2_out, driver_3_out, driver_4_out, driver_5_out, driver_6_out, driver_7_out, driver_8_out,
       driver_9_out, driver_10_out, driver_11_out, driver_12_out, driver_13_out, driver_14_out,
       driver_15_out, driver_16_out, jk_ff_as_1_nq, jk_ff_as_1_q, nor_1_out, nor_2_out, nor_3_out, nor_4_out,
       nor_5_out, nor_6_out, nor_7_out, nor_8_out, nor_9_out, nor_10_out, nor_11_out, nor_12_out, not_1_out,
       not_2_out, not_3_out, not_4_out, not_5_out, or_4_out;

  nor nor_1 (nor_1_out, in_8, in_9);
  nor nor_2 (nor_2_out, in_10, in_11);
  nor nor_3 (nor_3_out, in_4, in_5);
  nor nor_4 (nor_4_out, in_6, in_7);
  JK_FF_AS jk_ff_as_1 (.Set(~in_1), .J(in_1), .C(in_25), .K(in_1), .Clr(~in_1), .Q(jk_ff_as_1_q), .nQ(jk_ff_as_1_nq));
  and and_1 (out_2, in_25, jk_ff_as_1_q);
  and and_2 (out_3, jk_ff_as_1_nq, in_25);
  and and_3 (and_3_out, nor_1_out, nor_2_out);
  and and_4 (and_4_out, nor_3_out, nor_4_out);
  and and_5 (out_12, and_3_out, and_4_out);
  and and_6 (and_6_out, clk, in_132);
  and and_7 (and_7_out, ~in_132, in_133);  // And
  or or_1 (out_134, and_6_out, and_7_out);
  ROM #(.AddrBits(3), .Bits(4)) rom_1 (.A({in_15, in_14, in_13}), .sel(in_16), .D({out_24, out_23, out_22, out_21}));
  PullDown pulldown_1 (.out(out_24));
  PullDown pulldown_2 (.out(out_23));
  PullDown pulldown_3 (.out(out_22));
  D_FF #(.Bits(4)) d_ff_1 (
    .D({out_24, out_23, out_22, out_21}), .C(out_2), .Q({out_20, out_19, out_18, out_17}));  // open: nQ
  PullDown pulldown_4 (.out(out_21));
  assign driver_1_out = in_43 ? in_35 : 1'bz;  // Driver driver_1
  assign driver_2_out = in_43 ? in_36 : 1'bz;  // Driver driver_2
  assign driver_3_out = in_52 ? in_44 : 1'bz;  // Driver driver_3
  assign driver_4_out = in_52 ? in_45 : 1'bz;  // Driver driver_4
  PriorityEncoder #(.Selector_Bits(3)) TRAPS (
    .in0(in_118), .in1(in_119), .in2(in_120), .in3(in_121), .in4(in_122), .in5(in_123), .in6(in_124),
    .in7(in_125), .num(out_126), .any(out_127));
  assign driver_5_out = in_43 ? in_37 : 1'bz;  // Driver driver_5
  assign driver_6_out = in_43 ? in_38 : 1'bz;  // Driver driver_6
  assign driver_7_out = in_52 ? in_46 : 1'bz;  // Driver driver_7
  assign driver_8_out = in_52 ? in_47 : 1'bz;  // Driver driver_8
  assign driver_9_out = in_43 ? in_39 : 1'bz;  // Driver driver_9
  assign driver_10_out = in_43 ? in_40 : 1'bz;  // Driver driver_10
  assign driver_11_out = in_52 ? in_48 : 1'bz;  // Driver driver_11
  assign driver_12_out = in_52 ? in_49 : 1'bz;  // Driver driver_12
  assign driver_13_out = in_43 ? in_41 : 1'bz;  // Driver driver_13
  assign driver_14_out = in_43 ? in_42 : 1'bz;  // Driver driver_14
  assign driver_15_out = in_52 ? in_50 : 1'bz;  // Driver driver_15
  assign driver_16_out = in_52 ? in_51 : 1'bz;  // Driver driver_16
  PullDown pulldown_5 (.out(driver_1_out));
  PullDown pulldown_6 (.out(driver_9_out));
  PullDown pulldown_7 (.out(driver_6_out));
  PullDown pulldown_8 (.out(driver_5_out));
  PullDown pulldown_9 (.out(driver_2_out));
  PullDown pulldown_10 (.out(driver_8_out));
  PullDown pulldown_11 (.out(driver_7_out));
  PullDown pulldown_12 (.out(driver_4_out));
  PullDown pulldown_13 (.out(driver_3_out));
  nand nand_1 (out_130, in_128, in_129);
  PullDown pulldown_14 (.out(driver_14_out));
  PullDown pulldown_15 (.out(driver_13_out));
  PullDown pulldown_16 (.out(driver_10_out));
  PullDown pulldown_17 (.out(driver_16_out));
  PullDown pulldown_18 (.out(driver_15_out));
  PullDown pulldown_19 (.out(driver_12_out));
  PullDown pulldown_20 (.out(driver_11_out));
  and and_8 (out_90, nmemst_2, nsel_2);
  or or_2 (out_87, ~nmemst, nsel);  // Or
  // _74245 _74245_1: pin names not known; wires that end beside it: driver_1_out, driver_2_out, driver_3_out, driver_5_out, driver_4_out, driver_6_out, driver_7_out, driver_9_out, driver_8_out, driver_10_out, driver_11_out, driver_13_out, driver_12_out, driver_14_out, driver_15_out, 1'b0, driver_16_out, 1'b1, in_62, in_63
  assign out_32 = in_34 ? driver_13_out : 1'bz;  // Driver driver_17
  assign out_33 = in_34 ? driver_14_out : 1'bz;  // Driver driver_18
  assign out_60 = in_61 ? driver_16_out : 1'bz;  // Driver driver_19
  assign out_30 = in_34 ? driver_9_out : 1'bz;  // Driver driver_20
  assign out_31 = in_34 ? driver_10_out : 1'bz;  // Driver driver_21
  assign out_58 = in_61 ? driver_12_out : 1'bz;  // Driver driver_22
  assign out_59 = in_61 ? driver_15_out : 1'bz;  // Driver driver_23
  nor nor_5 (nor_5_out, in_102, in_103);
  nor nor_6 (nor_6_out, in_104, in_105);
  nor nor_7 (nor_7_out, in_106, in_107);
  nor nor_8 (nor_8_out, in_108, in_109);
  nor nor_9 (nor_9_out, in_110, in_111);
  nor nor_10 (nor_10_out, in_112, in_113);
  nor nor_11 (nor_11_out, in_114, in_115);
  nor nor_12 (nor_12_out, in_116, in_117);
  assign out_28 = in_34 ? driver_5_out : 1'bz;  // Driver driver_24
  assign out_29 = in_34 ? driver_6_out : 1'bz;  // Driver driver_25
  assign out_56 = in_61 ? driver_8_out : 1'bz;  // Driver driver_26
  assign out_57 = in_61 ? driver_11_out : 1'bz;  // Driver driver_27
  assign out_26 = in_34 ? driver_1_out : 1'bz;  // Driver driver_28
  assign out_27 = in_34 ? driver_2_out : 1'bz;  // Driver driver_29
  assign out_54 = in_61 ? driver_4_out : 1'bz;  // Driver driver_30
  assign out_55 = in_61 ? driver_7_out : 1'bz;  // Driver driver_31
  assign out_53 = in_61 ? driver_3_out : 1'bz;  // Driver driver_32
  PriorityEncoder #(.Selector_Bits(3)) TRAPS_2 (
    .in0(nor_5_out), .in1(nor_6_out), .in2(nor_7_out), .in3(nor_8_out), .in4(nor_9_out), .in5(nor_10_out),
    .in6(nor_11_out), .in7(nor_12_out), .num(out_100), .any(out_101));
  not not_1 (not_1_out, in_70);
  not not_2 (not_2_out, in_74);
  not not_3 (not_3_out, in_76);
  not not_4 (not_4_out, C);
  and and_9 (and_9_out, not_4_out, C_en);
  and and_10 (and_10_out, E, E_en);
  nor nor_13 (out_72, not_1_out, in_71);
  and and_11 (out_73, not_2_out, in_75);
  or or_3 (out_78, not_3_out, in_77);
  nand nand_2 (out_81, in_79, in_80);
  or or_4 (or_4_out, and_9_out, and_10_out);
  Multiplexer multiplexer_1 (.sel(in_66), .in_0(or_4_out), .in_1(not_5_out), .out(out_67));
  not not_5 (not_5_out, or_4_out);
  and and_12 (and_12_out, in_95, in_93);
  nand nand_3 (out_99, in_97, in_98);
  Add #(.Bits(8)) add_1 (.a(in_82), .b(in_83), .c_i(Ci), .s(out_85), .c_o(out_86));
  and and_13 (out_96, and_12_out, in_94);

  // Notes on the sheet:
  //   in_71: default 1
  //   in_75: default 1
  //   in_77: default 1
  //   in_80: default 1
  //   nmemst: default 1
  //   nsel: default 1
  //   nmemst_2: default 1
  //   nsel_2: default 1
  //   in_93: default 1
  //   in_94: default 1
  //   in_95: default 1
  //   in_97: default 1
  //   in_98: default 1
  //   in_102: default 1
  //   in_104: default 1
  //   in_106: default 1
  //   in_108: default 1
  //   in_110: default 1
  //   in_112: default 1
  //   in_114: default 1
  //   in_116: default 1
  //   in_118: default 1
  //   in_119: default 1
  //   in_120: default 1
  //   in_121: default 1
  //   in_122: default 1
  //   in_123: default 1
  //   in_124: default 1
  //   clk: Hz: 5
  //   2 PHASE CLOCK
  //   A=0
  //   contents of rom_1 (hex, n*v repeats v):
  //   1,2,3,4,5,6,7,8
endmodule
