// Digital circuit kjy.dig as structural Verilog
module kjy (
);

  wire _74181_1_p19, and_1_out, and_2_out, demultiplexer_1_out_1, demultiplexer_1_out_2,
       demultiplexer_1_out_3, demultiplexer_1_out_4, demultiplexer_1_out_5, demultiplexer_1_out_6,
       demultiplexer_1_out_7, demultiplexer_2_out_0, demultiplexer_2_out_1, demultiplexer_3_out_1,
       demultiplexer_3_out_2, demultiplexer_3_out_3, demultiplexer_3_out_4, demultiplexer_3_out_5,
       demultiplexer_3_out_6, demultiplexer_3_out_7, demultiplexer_4_out_0, multiplexer_2_out,
       multiplexer_3_out, nA_DOUT, nA_st, nB_DOUT, nB_st, nC_DOUT, nC_st, nIRQ_DOUT, nIRQ_st, nISR_st,
       nMAR_st, nMEM_DOUT, nMEM_st, nNZC_DOUT, nor_1_out, nor_2_out, nor_3_out, nor_4_out, not_4_out,
       not_5_out, nPC_DOUT, nPC_en, nPC_st, nSEQ_clr, nSEQ_en, nSUM_DOUT, nSUMF_st, undriven, undriven_2;
  wire [0:0] IRQ_q;
  wire [2:0] _74181_2_p18, _74245_1_p9, multiplexer_1_out, NZC_q;
  wire [3:0] _74181_1_p10, SEQ_out;
  wire [6:0] _74181_1_p15;
  wire [7:0] _256B_RAM_d, A_q, B_q, C_q, ISR_q, MAR_q, PC_out, SUM_q;
  wire [7:3] _74245_1_p12;
  wire [23:0] d_ff_1_q, rom_1_d;

  Register #(.Bits(8)) MAR (.D({_74245_1_p12, _74245_1_p9}), .en(~nMAR_st), .Q(MAR_q));  // open: C
  RAMSinglePortSel #(.AddrBits(8), .Bits(8)) _256B_RAM (
    .A(MAR_q), .WE(~nMEM_st), .OE(~nMEM_DOUT), .D(_256B_RAM_d));  // open: CS
  // _74245 _74245_1: pin names not known; wires that end beside it: _256B_RAM_d[0], _256B_RAM_d[1], _256B_RAM_d[2], _256B_RAM_d[3], _256B_RAM_d[4], _256B_RAM_d[5], _256B_RAM_d[6], _256B_RAM_d[7], _74245_1_p9[0], _74245_1_p9[1], _74245_1_p9[2], _74245_1_p12[3], _74245_1_p12[4], _74245_1_p12[5], _74245_1_p12[6], _74245_1_p12[7]
  Multiplexer #(.Bits(3)) multiplexer_1 (
    .in_0(_74181_2_p18), .in_1(_74245_1_p9), .out(multiplexer_1_out));  // open: sel
  Multiplexer multiplexer_2 (.in_1(_74245_1_p9[0]), .out(multiplexer_2_out));  // open: sel, in_0
  Register #(.Bits(8)) SUM (.D({_74181_2_p18[1], _74181_1_p15}), .en(~nSUMF_st), .Q(SUM_q));  // open: C
  assign _74245_1_p9[0] = ~nSUM_DOUT ? SUM_q[0] : 1'bz;  // DriverInvSel driverinvsel_1
  Register #(.Bits(8)) A (.D({_74245_1_p12, _74245_1_p9}), .en(~nA_st), .Q(A_q));  // open: C
  assign _74245_1_p9[0] = ~nA_DOUT ? A_q[0] : 1'bz;  // DriverInvSel driverinvsel_2
  Register #(.Bits(8)) ISR (.D({_74245_1_p12, _74245_1_p9}), .en(~nISR_st), .Q(ISR_q));  // open: C
  Register #(.Bits(8)) B (.D({_74245_1_p12, _74245_1_p9}), .en(~nB_st), .Q(B_q));  // open: C
  assign _74245_1_p9[0] = ~nB_DOUT ? B_q[0] : 1'bz;  // DriverInvSel driverinvsel_3
  Register #(.Bits(8)) C (.D({_74245_1_p12, _74245_1_p9}), .en(~nC_st), .Q(C_q));  // open: C
  assign _74245_1_p9[0] = ~nC_DOUT ? C_q[0] : 1'bz;  // DriverInvSel driverinvsel_4
  CounterPreset #(.Bits(8)) PC (
    .en(~nPC_en), .dir(1'b0), .in({_74245_1_p12, _74245_1_p9}), .ld(~nPC_st), .clr(1'b0), .out(PC_out));  // open: C, ovf
  assign _74245_1_p9[0] = ~nPC_DOUT ? PC_out[0] : 1'bz;  // DriverInvSel driverinvsel_5
  Register #(.Bits(3)) NZC (.D(multiplexer_1_out), .en(~nSUMF_st), .Q(NZC_q));  // open: C
  assign {_74245_1_p12, _74245_1_p9} = ~nNZC_DOUT ? {{5{1'b0}}, NZC_q} : 8'bz;  // DriverInvSel driverinvsel_6
  Register IRQ (.D(multiplexer_2_out), .en(~nIRQ_st), .Q(IRQ_q[0]));  // open: C
  assign {_74245_1_p12, _74245_1_p9} = ~nIRQ_DOUT ? {{7{1'b0}}, IRQ_q[0]} : 8'bz;  // DriverInvSel driverinvsel_7
  Multiplexer multiplexer_3 (.sel(undriven_2), .in_0(NZC_q[2]), .in_1(undriven), .out(multiplexer_3_out));
  ROM #(.AddrBits(16), .Bits(24)) rom_1 (.A({IRQ_q[0], NZC_q, ISR_q, SEQ_out}), .D(rom_1_d));  // open: sel
  CounterPreset #(.Bits(4)) SEQ (
    .en(~nSEQ_en), .dir(1'b0), .ld(~nSEQ_clr), .clr(1'b0), .out(SEQ_out));  // open: C, in, ovf
  // _74181 _74181_1: pin names not known; wires that end beside it: multiplexer_3_out, A_q[0], A_q[1], A_q[2], A_q[3], _74245_1_p9[0], _74245_1_p9[1], _74245_1_p9[2], _74245_1_p12[3], _74181_1_p10[0], _74181_1_p10[1], _74181_1_p10[2], _74181_1_p10[3], d_ff_1_q[12], _74181_1_p15[0], _74181_1_p15[1], _74181_1_p15[2], _74181_1_p15[3], _74181_1_p19
  // _74181 _74181_2: pin names not known; wires that end beside it: _74181_1_p19, A_q[4], A_q[5], A_q[6], A_q[7], _74245_1_p12[4], _74245_1_p12[5], _74245_1_p12[6], _74245_1_p12[7], _74181_1_p10[0], _74181_1_p10[1], _74181_1_p10[2], _74181_1_p10[3], d_ff_1_q[12], _74181_1_p15[4], _74181_1_p15[5], _74181_1_p15[6], _74181_2_p18[1], _74181_2_p18[2]
  D_FF #(.Bits(24)) d_ff_1 (.D(rom_1_d), .Q({d_ff_1_q[23:12], _74181_1_p10, d_ff_1_q[7:0]}));  // open: C, nQ
  not not_1 (nPC_en, d_ff_1_q[13]);
  not not_2 (nSEQ_en, d_ff_1_q[14]);
  not not_3 (nSEQ_clr, d_ff_1_q[15]);
  Demultiplexer #(.Selector_Bits(3)) demultiplexer_1 (
    .sel(d_ff_1_q[2:0]), .in(not_4_out), .out_1(demultiplexer_1_out_1), .out_2(demultiplexer_1_out_2),
    .out_3(demultiplexer_1_out_3), .out_4(demultiplexer_1_out_4), .out_5(demultiplexer_1_out_5),
    .out_6(demultiplexer_1_out_6), .out_7(demultiplexer_1_out_7));  // open: out_0
  not not_4 (not_4_out, d_ff_1_q[3]);
  Demultiplexer #(.Selector_Bits(3)) demultiplexer_2 (
    .sel(d_ff_1_q[2:0]), .in(d_ff_1_q[3]), .out_0(demultiplexer_2_out_0), .out_1(demultiplexer_2_out_1));  // open: out_2, out_3, out_4, out_5, out_6, out_7
  Demultiplexer #(.Selector_Bits(3)) demultiplexer_3 (
    .sel(d_ff_1_q[6:4]), .in(not_5_out), .out_1(demultiplexer_3_out_1), .out_2(demultiplexer_3_out_2),
    .out_3(demultiplexer_3_out_3), .out_4(demultiplexer_3_out_4), .out_5(demultiplexer_3_out_5),
    .out_6(demultiplexer_3_out_6), .out_7(demultiplexer_3_out_7));  // open: out_0
  not not_5 (not_5_out, d_ff_1_q[7]);
  Demultiplexer #(.Selector_Bits(3)) demultiplexer_4 (
    .sel(d_ff_1_q[6:4]), .in(d_ff_1_q[7]), .out_0(demultiplexer_4_out_0));  // open: out_1, out_2, out_3, out_4, out_5, out_6, out_7
  nor nor_1 (nor_1_out, _74181_1_p15[0], _74181_1_p15[1]);
  nor nor_2 (nor_2_out, _74181_1_p15[2], _74181_1_p15[3]);
  nor nor_3 (nor_3_out, _74181_1_p15[4], _74181_1_p15[5]);
  nor nor_4 (nor_4_out, _74181_1_p15[6], _74181_2_p18[1]);
  not not_6 (nA_st, demultiplexer_1_out_1);
  not not_7 (nB_st, demultiplexer_1_out_2);
  not not_8 (nC_st, demultiplexer_1_out_3);
  not not_9 (nPC_st, demultiplexer_1_out_4);
  not not_10 (nISR_st, demultiplexer_1_out_5);
  not not_11 (nMAR_st, demultiplexer_1_out_6);
  not not_12 (nMEM_st, demultiplexer_1_out_7);
  not not_13 (nIRQ_st, demultiplexer_2_out_0);
  not not_14 (nSUMF_st, demultiplexer_2_out_1);
  not not_15 (nA_DOUT, demultiplexer_3_out_1);
  not not_16 (nB_DOUT, demultiplexer_3_out_2);
  not not_17 (nC_DOUT, demultiplexer_3_out_3);
  not not_18 (nPC_DOUT, demultiplexer_3_out_4);
  not not_19 (nMEM_DOUT, demultiplexer_3_out_5);
  not not_20 (nIRQ_DOUT, demultiplexer_3_out_6);
  not not_21 (nSUM_DOUT, demultiplexer_3_out_7);
  not not_22 (nNZC_DOUT, demultiplexer_4_out_0);
  and and_1 (and_1_out, nor_1_out, nor_2_out);
  and and_2 (and_2_out, nor_3_out, nor_4_out);
  and and_3 (_74181_2_p18[0], and_1_out, and_2_out);
  // Pins of 1 and 5 bits meet at {5{1'b0}}
  // Pins of 1 and 8 bits meet at {_74245_1_p12, _74245_1_p9}
  // Pins of 1 and 5 bits meet at {5{1'b0}}
  // Pins of 1 and 8 bits meet at PC_out
  // Pins of 1 and 8 bits meet at B_q
  // Pins of 1 and 8 bits meet at A_q
  // Pins of 1 and 8 bits meet at C_q
  // Pins of 1 and 5 bits meet at {5{1'b0}}
  // Pins of 1 and 5 bits meet at {5{1'b0}}
  // Pins of 1 and 8 bits meet at SUM_q
  // Pins of 16 and 24 bits meet at {d_ff_1_q[23:12], _74181_1_p10, d_ff_1_q[7:0]}
endmodule
